// Logisim project cpu_control_unit_base.circ as structural Verilog
module main (
  input  [7:0] in_1,
  input  [7:0] in_2,
  input  in_3,
  output [7:0] out_4
);

  RAM #(.bus("separate")) ram_1 (.addr(in_1), .din(in_2), .data(out_4), .clk(in_3));  // open: str, sel, ld, clr
endmodule

module cpu_memory_1 (
  input  in_1,
  input  in_2,
  output out_3
);

  wire nand_1_out, nand_2_out, nand_4_out;

  nand nand_1 (nand_1_out, in_1, in_2);
  nand nand_2 (nand_2_out, nand_1_out, in_2);
  nand nand_3 (out_3, nand_1_out, nand_4_out);
  nand nand_4 (nand_4_out, out_3, nand_2_out);

  // Notes on the sheet:
  //   in_1: pull=down
  //   out_3: pull=up
  //   in_2: pull=down
endmodule

module cpu_mem_8 (
  input  [7:0] in_1,
  input  in_2,
  output [7:0] out_3
);

  cpu_memory_1 cpu_memory_1_1 (.in_1(in_1[0]), .out_3(out_3[0]), .in_2(in_2));
  cpu_memory_1 cpu_memory_1_2 (.in_1(in_1[1]), .out_3(out_3[1]), .in_2(in_2));
  cpu_memory_1 cpu_memory_1_3 (.in_1(in_1[2]), .out_3(out_3[2]), .in_2(in_2));
  cpu_memory_1 cpu_memory_1_4 (.in_1(in_1[3]), .out_3(out_3[3]), .in_2(in_2));
  cpu_memory_1 cpu_memory_1_5 (.in_1(in_1[4]), .out_3(out_3[4]), .in_2(in_2));
  cpu_memory_1 cpu_memory_1_6 (.in_1(in_1[5]), .out_3(out_3[5]), .in_2(in_2));
  cpu_memory_1 cpu_memory_1_7 (.in_1(in_1[6]), .out_3(out_3[6]), .in_2(in_2));
  cpu_memory_1 cpu_memory_1_8 (.in_1(in_1[7]), .out_3(out_3[7]), .in_2(in_2));
endmodule

module cpu_eneb_8 (
  input  [7:0] in_1,
  input  in_2,
  output [7:0] out_3
);

  and and_1 (out_3[0], in_1[0], in_2);
  and and_2 (out_3[1], in_1[1], in_2);
  and and_3 (out_3[2], in_1[2], in_2);
  and and_4 (out_3[3], in_1[3], in_2);
  and and_5 (out_3[4], in_1[4], in_2);
  and and_6 (out_3[5], in_1[5], in_2);
  and and_7 (out_3[6], in_1[6], in_2);
  and and_8 (out_3[7], in_1[7], in_2);
endmodule

module cpu_register_8 (
  input  [7:0] in_1,
  input  s,
  input  e,
  output [7:0] out_4,
  output [7:0] out_5
);

  wire [7:0] cpu_eneb_8_1_out_3;

  cpu_mem_8 cpu_mem_8_1 (.in_1(in_1), .out_3(out_4), .in_2(s));
  cpu_eneb_8 cpu_eneb_8_1 (.in_1(out_4), .out_3(cpu_eneb_8_1_out_3), .in_2(e));
  assign out_5 = e ? cpu_eneb_8_1_out_3 : 8'bz;  // Controlled_Buffer controlled_buffer_1
endmodule

module cpu_decoder_2x4 (
  input  in_1,
  input  in_2,
  output out_3,
  output out_4,
  output out_5,
  output out_6
);

  wire not_1_out, not_2_out;

  not not_1 (not_1_out, in_2);
  not not_2 (not_2_out, in_1);
  and and_1 (out_3, not_2_out, not_1_out);
  and and_2 (out_4, not_2_out, in_2);
  and and_3 (out_5, in_1, not_1_out);
  and and_4 (out_6, in_1, in_2);
endmodule

module cpu_decoder_3x8 (
  input  [2:0] in_1,
  output out_2,
  output out_3,
  output out_4,
  output out_5,
  output out_6,
  output out_7,
  output out_8,
  output out_9
);

  wire not_1_out, not_2_out, not_3_out;

  not not_1 (not_1_out, in_1[2]);
  not not_2 (not_2_out, in_1[1]);
  not not_3 (not_3_out, in_1[0]);
  and and_1 (out_2, not_3_out, not_2_out, not_1_out);
  and and_2 (out_3, in_1[0], not_2_out, not_1_out);
  and and_3 (out_4, not_3_out, in_1[1], not_1_out);
  and and_4 (out_5, in_1[0], in_1[1], not_1_out);
  and and_5 (out_6, not_3_out, not_2_out, in_1[2]);
  and and_6 (out_7, in_1[0], not_2_out, in_1[2]);
  and and_7 (out_8, not_3_out, in_1[1], in_1[2]);
  and and_8 (out_9, in_1[0], in_1[1], in_1[2]);
endmodule

module cpu_reg_byte (
  input  [7:0] in_1,
  input  in_2,
  input  h,
  input  v,
  input  s,
  input  e,
  output [7:0] out_7,
  output [7:0] out_8
);

  wire and_1_out, and_2_out, and_3_out, or_1_out;
  wire [7:0] cpu_register_8_1_out_5;

  and and_1 (and_1_out, h, v);
  and and_2 (and_2_out, and_1_out, s);
  and and_3 (and_3_out, and_1_out, e);
  or or_1 (or_1_out, in_2, and_2_out);
  cpu_register_8 cpu_register_8_1 (
    .in_1(in_1), .out_5(cpu_register_8_1_out_5), .s(or_1_out), .e(and_3_out), .out_4(out_8));
  assign out_7 = and_3_out ? cpu_register_8_1_out_5 : 8'bz;  // Controlled_Buffer controlled_buffer_1

  // Notes on the sheet:
  //   reset
endmodule

module cpu_ram_256_example (
  input  in_1,
  input  [7:0] in_2,
  input  in_3,
  input  [7:0] in_4,
  input  s,
  input  e,
  output [7:0] out_7,
  output [7:0] out_8
);

  wire cpu_decoder_4x16_1_out_2, cpu_decoder_4x16_2_out_17;
  wire [7:0] cpu_mem_8_1_out_3, cpu_reg_byte_1_out_7;

  cpu_mem_8 cpu_mem_8_1 (.in_1(in_4), .out_3(cpu_mem_8_1_out_3), .in_2(in_3));
  cpu_decoder_4x16 cpu_decoder_4x16_1 (
    .in_1(cpu_mem_8_1_out_3[7:4]), .out_2(cpu_decoder_4x16_1_out_2));  // open: out_3, out_4, out_5, out_6, out_7, out_8, out_9, out_10, out_11, out_12, out_13, out_14, out_15, out_16, out_17
  assign out_7 = e ? cpu_reg_byte_1_out_7 : 8'bz;  // Controlled_Buffer controlled_buffer_1
  cpu_reg_byte cpu_reg_byte_1 (
    .out_8(out_8), .in_2(in_1), .h(cpu_decoder_4x16_1_out_2), .v(cpu_decoder_4x16_2_out_17), .in_1(in_2),
    .out_7(cpu_reg_byte_1_out_7), .s(s), .e(e));
  cpu_decoder_4x16 cpu_decoder_4x16_2 (
    .in_1(cpu_mem_8_1_out_3[3:0]), .out_17(cpu_decoder_4x16_2_out_17));  // open: out_2, out_3, out_4, out_5, out_6, out_7, out_8, out_9, out_10, out_11, out_12, out_13, out_14, out_15, out_16
endmodule

module cpu_decoder_4x16 (
  input  [3:0] in_1,
  output out_2,
  output out_3,
  output out_4,
  output out_5,
  output out_6,
  output out_7,
  output out_8,
  output out_9,
  output out_10,
  output out_11,
  output out_12,
  output out_13,
  output out_14,
  output out_15,
  output out_16,
  output out_17
);

  wire not_1_out, not_2_out, not_3_out, not_4_out;

  not not_1 (not_1_out, in_1[3]);
  not not_2 (not_2_out, in_1[2]);
  not not_3 (not_3_out, in_1[1]);
  not not_4 (not_4_out, in_1[0]);
  and and_1 (out_2, not_4_out, not_3_out, not_2_out, not_1_out);
  and and_2 (out_3, in_1[0], not_3_out, not_2_out, not_1_out);
  and and_3 (out_4, not_4_out, in_1[1], not_2_out, not_1_out);
  and and_4 (out_5, in_1[0], in_1[1], not_2_out, not_1_out);
  and and_5 (out_6, not_4_out, not_3_out, in_1[2], not_1_out);
  and and_6 (out_7, in_1[0], not_3_out, in_1[2], not_1_out);
  and and_7 (out_8, not_4_out, in_1[1], in_1[2], not_1_out);
  and and_8 (out_9, in_1[0], in_1[1], in_1[2], not_1_out);
  and and_9 (out_10, not_4_out, not_3_out, not_2_out, in_1[3]);
  and and_10 (out_11, in_1[0], not_3_out, not_2_out, in_1[3]);
  and and_11 (out_12, not_4_out, in_1[1], not_2_out, in_1[3]);
  and and_12 (out_13, in_1[0], in_1[1], not_2_out, in_1[3]);
  and and_13 (out_14, not_4_out, not_3_out, in_1[2], in_1[3]);
  and and_14 (out_15, in_1[0], not_3_out, in_1[2], in_1[3]);
  and and_15 (out_16, not_4_out, in_1[1], in_1[2], in_1[3]);
  and and_16 (out_17, in_1[0], in_1[1], in_1[2], in_1[3]);
endmodule

module my_ram_example (
  input  [7:0] in_1,
  input  s,
  input  in_3,
  input  e,
  output [7:0] out_5
);

  wire demultiplexer_1_out0, demultiplexer_1_out1;
  wire [7:0] multiplexer_1_out, register_1_q, register_2_q;

  Demultiplexer demultiplexer_1 (
    .out0(demultiplexer_1_out0), .out1(demultiplexer_1_out1), .in(s), .sel(in_3));  // open: en
  Register register_1 (.D(in_1), .Q(register_1_q), .clk(demultiplexer_1_out0));  // open: en, clr
  Register register_2 (.D(in_1), .Q(register_2_q), .clk(demultiplexer_1_out1));  // open: en, clr
  Multiplexer #(.width(8)) multiplexer_1 (
    .in0(register_1_q), .in1(register_2_q), .out(multiplexer_1_out), .sel(in_3));  // open: en
  assign out_5 = e ? multiplexer_1_out : 8'bz;  // Controlled_Buffer controlled_buffer_1

  // Notes on the sheet:
  //   address
endmodule

module my_ram_256 (
  input  [7:0] \input ,
  input  [7:0] in_2,
  input  reset,
  input  sa,
  input  s,
  input  e,
  output [7:0] \output 
);

  wire cpu_decoder_4x16_1_out_2, cpu_decoder_4x16_2_out_2, cpu_decoder_4x16_2_out_3,
       cpu_decoder_4x16_2_out_4, cpu_decoder_4x16_2_out_5, cpu_decoder_4x16_2_out_6,
       cpu_decoder_4x16_2_out_7, cpu_decoder_4x16_2_out_8, cpu_decoder_4x16_2_out_9,
       cpu_decoder_4x16_2_out_10, cpu_decoder_4x16_2_out_11, cpu_decoder_4x16_2_out_12,
       cpu_decoder_4x16_2_out_13, cpu_decoder_4x16_2_out_14, cpu_decoder_4x16_2_out_15,
       cpu_decoder_4x16_2_out_16, cpu_decoder_4x16_2_out_17;
  wire [7:0] cpu_mem_8_1_out_3, cpu_reg_byte_1_out_7;

  cpu_mem_8 cpu_mem_8_1 (.in_1(in_2), .out_3(cpu_mem_8_1_out_3), .in_2(sa));
  assign \output  = e ? cpu_reg_byte_1_out_7 : 8'bz;  // Controlled_Buffer controlled_buffer_1
  cpu_decoder_4x16 cpu_decoder_4x16_1 (
    .in_1(cpu_mem_8_1_out_3[7:4]), .out_2(cpu_decoder_4x16_1_out_2));  // open: out_3, out_4, out_5, out_6, out_7, out_8, out_9, out_10, out_11, out_12, out_13, out_14, out_15, out_16, out_17
  cpu_reg_byte cpu_reg_byte_1 (
    .in_2(reset), .h(cpu_decoder_4x16_1_out_2), .v(cpu_decoder_4x16_2_out_17), .in_1(\input ),
    .out_7(cpu_reg_byte_1_out_7), .s(s), .e(e));  // open: out_8
  cpu_reg_byte cpu_reg_byte_2 ();  // open: out_8, in_2, h, v, in_1, out_7, s, e
  cpu_reg_byte cpu_reg_byte_3 ();  // open: out_8, in_2, h, v, in_1, out_7, s, e
  cpu_reg_byte cpu_reg_byte_4 ();  // open: out_8, in_2, h, v, in_1, out_7, s, e
  cpu_reg_byte cpu_reg_byte_5 ();  // open: out_8, in_2, h, v, in_1, out_7, s, e
  cpu_reg_byte cpu_reg_byte_6 ();  // open: out_8, in_2, h, v, in_1, out_7, s, e
  cpu_reg_byte cpu_reg_byte_7 ();  // open: out_8, in_2, h, v, in_1, out_7, s, e
  cpu_reg_byte cpu_reg_byte_8 ();  // open: out_8, in_2, h, v, in_1, out_7, s, e
  cpu_reg_byte cpu_reg_byte_9 ();  // open: out_8, in_2, h, v, in_1, out_7, s, e
  cpu_reg_byte cpu_reg_byte_10 ();  // open: out_8, in_2, h, v, in_1, out_7, s, e
  cpu_reg_byte cpu_reg_byte_11 ();  // open: out_8, in_2, h, v, in_1, out_7, s, e
  cpu_reg_byte cpu_reg_byte_12 ();  // open: out_8, in_2, h, v, in_1, out_7, s, e
  cpu_reg_byte cpu_reg_byte_13 ();  // open: out_8, in_2, h, v, in_1, out_7, s, e
  cpu_reg_byte cpu_reg_byte_14 ();  // open: out_8, in_2, h, v, in_1, out_7, s, e
  cpu_reg_byte cpu_reg_byte_15 ();  // open: out_8, in_2, h, v, in_1, out_7, s, e
  cpu_reg_byte cpu_reg_byte_16 ();  // open: out_8, in_2, h, v, in_1, out_7, s, e
  cpu_reg_byte cpu_reg_byte_17 (
    .in_2(reset), .h(cpu_decoder_4x16_1_out_2), .v(cpu_decoder_4x16_2_out_16), .in_1(\input ),
    .out_7(cpu_reg_byte_1_out_7), .s(s), .e(e));  // open: out_8
  cpu_reg_byte cpu_reg_byte_18 ();  // open: out_8, in_2, h, v, in_1, out_7, s, e
  cpu_reg_byte cpu_reg_byte_19 ();  // open: out_8, in_2, h, v, in_1, out_7, s, e
  cpu_reg_byte cpu_reg_byte_20 ();  // open: out_8, in_2, h, v, in_1, out_7, s, e
  cpu_reg_byte cpu_reg_byte_21 ();  // open: out_8, in_2, h, v, in_1, out_7, s, e
  cpu_reg_byte cpu_reg_byte_22 ();  // open: out_8, in_2, h, v, in_1, out_7, s, e
  cpu_reg_byte cpu_reg_byte_23 ();  // open: out_8, in_2, h, v, in_1, out_7, s, e
  cpu_reg_byte cpu_reg_byte_24 ();  // open: out_8, in_2, h, v, in_1, out_7, s, e
  cpu_reg_byte cpu_reg_byte_25 ();  // open: out_8, in_2, h, v, in_1, out_7, s, e
  cpu_reg_byte cpu_reg_byte_26 ();  // open: out_8, in_2, h, v, in_1, out_7, s, e
  cpu_reg_byte cpu_reg_byte_27 ();  // open: out_8, in_2, h, v, in_1, out_7, s, e
  cpu_reg_byte cpu_reg_byte_28 ();  // open: out_8, in_2, h, v, in_1, out_7, s, e
  cpu_reg_byte cpu_reg_byte_29 ();  // open: out_8, in_2, h, v, in_1, out_7, s, e
  cpu_reg_byte cpu_reg_byte_30 ();  // open: out_8, in_2, h, v, in_1, out_7, s, e
  cpu_reg_byte cpu_reg_byte_31 ();  // open: out_8, in_2, h, v, in_1, out_7, s, e
  cpu_reg_byte cpu_reg_byte_32 ();  // open: out_8, in_2, h, v, in_1, out_7, s, e
  cpu_reg_byte cpu_reg_byte_33 (
    .in_2(reset), .h(cpu_decoder_4x16_1_out_2), .v(cpu_decoder_4x16_2_out_15), .in_1(\input ),
    .out_7(cpu_reg_byte_1_out_7), .s(s), .e(e));  // open: out_8
  cpu_reg_byte cpu_reg_byte_34 ();  // open: out_8, in_2, h, v, in_1, out_7, s, e
  cpu_reg_byte cpu_reg_byte_35 ();  // open: out_8, in_2, h, v, in_1, out_7, s, e
  cpu_reg_byte cpu_reg_byte_36 ();  // open: out_8, in_2, h, v, in_1, out_7, s, e
  cpu_reg_byte cpu_reg_byte_37 ();  // open: out_8, in_2, h, v, in_1, out_7, s, e
  cpu_reg_byte cpu_reg_byte_38 ();  // open: out_8, in_2, h, v, in_1, out_7, s, e
  cpu_reg_byte cpu_reg_byte_39 ();  // open: out_8, in_2, h, v, in_1, out_7, s, e
  cpu_reg_byte cpu_reg_byte_40 ();  // open: out_8, in_2, h, v, in_1, out_7, s, e
  cpu_reg_byte cpu_reg_byte_41 ();  // open: out_8, in_2, h, v, in_1, out_7, s, e
  cpu_reg_byte cpu_reg_byte_42 ();  // open: out_8, in_2, h, v, in_1, out_7, s, e
  cpu_reg_byte cpu_reg_byte_43 ();  // open: out_8, in_2, h, v, in_1, out_7, s, e
  cpu_reg_byte cpu_reg_byte_44 ();  // open: out_8, in_2, h, v, in_1, out_7, s, e
  cpu_reg_byte cpu_reg_byte_45 ();  // open: out_8, in_2, h, v, in_1, out_7, s, e
  cpu_reg_byte cpu_reg_byte_46 ();  // open: out_8, in_2, h, v, in_1, out_7, s, e
  cpu_reg_byte cpu_reg_byte_47 ();  // open: out_8, in_2, h, v, in_1, out_7, s, e
  cpu_reg_byte cpu_reg_byte_48 ();  // open: out_8, in_2, h, v, in_1, out_7, s, e
  cpu_reg_byte cpu_reg_byte_49 (
    .in_2(reset), .h(cpu_decoder_4x16_1_out_2), .v(cpu_decoder_4x16_2_out_14), .in_1(\input ),
    .out_7(cpu_reg_byte_1_out_7), .s(s), .e(e));  // open: out_8
  cpu_reg_byte cpu_reg_byte_50 ();  // open: out_8, in_2, h, v, in_1, out_7, s, e
  cpu_reg_byte cpu_reg_byte_51 ();  // open: out_8, in_2, h, v, in_1, out_7, s, e
  cpu_reg_byte cpu_reg_byte_52 ();  // open: out_8, in_2, h, v, in_1, out_7, s, e
  cpu_reg_byte cpu_reg_byte_53 ();  // open: out_8, in_2, h, v, in_1, out_7, s, e
  cpu_reg_byte cpu_reg_byte_54 ();  // open: out_8, in_2, h, v, in_1, out_7, s, e
  cpu_reg_byte cpu_reg_byte_55 ();  // open: out_8, in_2, h, v, in_1, out_7, s, e
  cpu_reg_byte cpu_reg_byte_56 ();  // open: out_8, in_2, h, v, in_1, out_7, s, e
  cpu_reg_byte cpu_reg_byte_57 ();  // open: out_8, in_2, h, v, in_1, out_7, s, e
  cpu_reg_byte cpu_reg_byte_58 ();  // open: out_8, in_2, h, v, in_1, out_7, s, e
  cpu_reg_byte cpu_reg_byte_59 ();  // open: out_8, in_2, h, v, in_1, out_7, s, e
  cpu_reg_byte cpu_reg_byte_60 ();  // open: out_8, in_2, h, v, in_1, out_7, s, e
  cpu_reg_byte cpu_reg_byte_61 ();  // open: out_8, in_2, h, v, in_1, out_7, s, e
  cpu_reg_byte cpu_reg_byte_62 ();  // open: out_8, in_2, h, v, in_1, out_7, s, e
  cpu_reg_byte cpu_reg_byte_63 ();  // open: out_8, in_2, h, v, in_1, out_7, s, e
  cpu_reg_byte cpu_reg_byte_64 ();  // open: out_8, in_2, h, v, in_1, out_7, s, e
  cpu_decoder_4x16 cpu_decoder_4x16_2 (
    .in_1(cpu_mem_8_1_out_3[3:0]), .out_2(cpu_decoder_4x16_2_out_2), .out_3(cpu_decoder_4x16_2_out_3),
    .out_4(cpu_decoder_4x16_2_out_4), .out_5(cpu_decoder_4x16_2_out_5), .out_6(cpu_decoder_4x16_2_out_6),
    .out_7(cpu_decoder_4x16_2_out_7), .out_8(cpu_decoder_4x16_2_out_8), .out_9(cpu_decoder_4x16_2_out_9),
    .out_10(cpu_decoder_4x16_2_out_10), .out_11(cpu_decoder_4x16_2_out_11),
    .out_12(cpu_decoder_4x16_2_out_12), .out_13(cpu_decoder_4x16_2_out_13),
    .out_14(cpu_decoder_4x16_2_out_14), .out_15(cpu_decoder_4x16_2_out_15),
    .out_16(cpu_decoder_4x16_2_out_16), .out_17(cpu_decoder_4x16_2_out_17));
  cpu_reg_byte cpu_reg_byte_65 (
    .in_2(reset), .h(cpu_decoder_4x16_1_out_2), .v(cpu_decoder_4x16_2_out_13), .in_1(\input ),
    .out_7(cpu_reg_byte_1_out_7), .s(s), .e(e));  // open: out_8
  cpu_reg_byte cpu_reg_byte_66 ();  // open: out_8, in_2, h, v, in_1, out_7, s, e
  cpu_reg_byte cpu_reg_byte_67 ();  // open: out_8, in_2, h, v, in_1, out_7, s, e
  cpu_reg_byte cpu_reg_byte_68 ();  // open: out_8, in_2, h, v, in_1, out_7, s, e
  cpu_reg_byte cpu_reg_byte_69 ();  // open: out_8, in_2, h, v, in_1, out_7, s, e
  cpu_reg_byte cpu_reg_byte_70 ();  // open: out_8, in_2, h, v, in_1, out_7, s, e
  cpu_reg_byte cpu_reg_byte_71 ();  // open: out_8, in_2, h, v, in_1, out_7, s, e
  cpu_reg_byte cpu_reg_byte_72 ();  // open: out_8, in_2, h, v, in_1, out_7, s, e
  cpu_reg_byte cpu_reg_byte_73 ();  // open: out_8, in_2, h, v, in_1, out_7, s, e
  cpu_reg_byte cpu_reg_byte_74 ();  // open: out_8, in_2, h, v, in_1, out_7, s, e
  cpu_reg_byte cpu_reg_byte_75 ();  // open: out_8, in_2, h, v, in_1, out_7, s, e
  cpu_reg_byte cpu_reg_byte_76 ();  // open: out_8, in_2, h, v, in_1, out_7, s, e
  cpu_reg_byte cpu_reg_byte_77 ();  // open: out_8, in_2, h, v, in_1, out_7, s, e
  cpu_reg_byte cpu_reg_byte_78 ();  // open: out_8, in_2, h, v, in_1, out_7, s, e
  cpu_reg_byte cpu_reg_byte_79 ();  // open: out_8, in_2, h, v, in_1, out_7, s, e
  cpu_reg_byte cpu_reg_byte_80 ();  // open: out_8, in_2, h, v, in_1, out_7, s, e
  cpu_reg_byte cpu_reg_byte_81 (
    .in_2(reset), .h(cpu_decoder_4x16_1_out_2), .v(cpu_decoder_4x16_2_out_12), .in_1(\input ),
    .out_7(cpu_reg_byte_1_out_7), .s(s), .e(e));  // open: out_8
  cpu_reg_byte cpu_reg_byte_82 ();  // open: out_8, in_2, h, v, in_1, out_7, s, e
  cpu_reg_byte cpu_reg_byte_83 ();  // open: out_8, in_2, h, v, in_1, out_7, s, e
  cpu_reg_byte cpu_reg_byte_84 ();  // open: out_8, in_2, h, v, in_1, out_7, s, e
  cpu_reg_byte cpu_reg_byte_85 ();  // open: out_8, in_2, h, v, in_1, out_7, s, e
  cpu_reg_byte cpu_reg_byte_86 ();  // open: out_8, in_2, h, v, in_1, out_7, s, e
  cpu_reg_byte cpu_reg_byte_87 ();  // open: out_8, in_2, h, v, in_1, out_7, s, e
  cpu_reg_byte cpu_reg_byte_88 ();  // open: out_8, in_2, h, v, in_1, out_7, s, e
  cpu_reg_byte cpu_reg_byte_89 ();  // open: out_8, in_2, h, v, in_1, out_7, s, e
  cpu_reg_byte cpu_reg_byte_90 ();  // open: out_8, in_2, h, v, in_1, out_7, s, e
  cpu_reg_byte cpu_reg_byte_91 ();  // open: out_8, in_2, h, v, in_1, out_7, s, e
  cpu_reg_byte cpu_reg_byte_92 ();  // open: out_8, in_2, h, v, in_1, out_7, s, e
  cpu_reg_byte cpu_reg_byte_93 ();  // open: out_8, in_2, h, v, in_1, out_7, s, e
  cpu_reg_byte cpu_reg_byte_94 ();  // open: out_8, in_2, h, v, in_1, out_7, s, e
  cpu_reg_byte cpu_reg_byte_95 ();  // open: out_8, in_2, h, v, in_1, out_7, s, e
  cpu_reg_byte cpu_reg_byte_96 ();  // open: out_8, in_2, h, v, in_1, out_7, s, e
  cpu_reg_byte cpu_reg_byte_97 (
    .in_2(reset), .h(cpu_decoder_4x16_1_out_2), .v(cpu_decoder_4x16_2_out_11), .in_1(\input ),
    .out_7(cpu_reg_byte_1_out_7), .s(s), .e(e));  // open: out_8
  cpu_reg_byte cpu_reg_byte_98 ();  // open: out_8, in_2, h, v, in_1, out_7, s, e
  cpu_reg_byte cpu_reg_byte_99 ();  // open: out_8, in_2, h, v, in_1, out_7, s, e
  cpu_reg_byte cpu_reg_byte_100 ();  // open: out_8, in_2, h, v, in_1, out_7, s, e
  cpu_reg_byte cpu_reg_byte_101 ();  // open: out_8, in_2, h, v, in_1, out_7, s, e
  cpu_reg_byte cpu_reg_byte_102 ();  // open: out_8, in_2, h, v, in_1, out_7, s, e
  cpu_reg_byte cpu_reg_byte_103 ();  // open: out_8, in_2, h, v, in_1, out_7, s, e
  cpu_reg_byte cpu_reg_byte_104 ();  // open: out_8, in_2, h, v, in_1, out_7, s, e
  cpu_reg_byte cpu_reg_byte_105 ();  // open: out_8, in_2, h, v, in_1, out_7, s, e
  cpu_reg_byte cpu_reg_byte_106 ();  // open: out_8, in_2, h, v, in_1, out_7, s, e
  cpu_reg_byte cpu_reg_byte_107 ();  // open: out_8, in_2, h, v, in_1, out_7, s, e
  cpu_reg_byte cpu_reg_byte_108 ();  // open: out_8, in_2, h, v, in_1, out_7, s, e
  cpu_reg_byte cpu_reg_byte_109 ();  // open: out_8, in_2, h, v, in_1, out_7, s, e
  cpu_reg_byte cpu_reg_byte_110 ();  // open: out_8, in_2, h, v, in_1, out_7, s, e
  cpu_reg_byte cpu_reg_byte_111 ();  // open: out_8, in_2, h, v, in_1, out_7, s, e
  cpu_reg_byte cpu_reg_byte_112 ();  // open: out_8, in_2, h, v, in_1, out_7, s, e
  cpu_reg_byte cpu_reg_byte_113 (
    .in_2(reset), .h(cpu_decoder_4x16_1_out_2), .v(cpu_decoder_4x16_2_out_10), .in_1(\input ),
    .out_7(cpu_reg_byte_1_out_7), .s(s), .e(e));  // open: out_8
  cpu_reg_byte cpu_reg_byte_114 ();  // open: out_8, in_2, h, v, in_1, out_7, s, e
  cpu_reg_byte cpu_reg_byte_115 ();  // open: out_8, in_2, h, v, in_1, out_7, s, e
  cpu_reg_byte cpu_reg_byte_116 ();  // open: out_8, in_2, h, v, in_1, out_7, s, e
  cpu_reg_byte cpu_reg_byte_117 ();  // open: out_8, in_2, h, v, in_1, out_7, s, e
  cpu_reg_byte cpu_reg_byte_118 ();  // open: out_8, in_2, h, v, in_1, out_7, s, e
  cpu_reg_byte cpu_reg_byte_119 ();  // open: out_8, in_2, h, v, in_1, out_7, s, e
  cpu_reg_byte cpu_reg_byte_120 ();  // open: out_8, in_2, h, v, in_1, out_7, s, e
  cpu_reg_byte cpu_reg_byte_121 ();  // open: out_8, in_2, h, v, in_1, out_7, s, e
  cpu_reg_byte cpu_reg_byte_122 ();  // open: out_8, in_2, h, v, in_1, out_7, s, e
  cpu_reg_byte cpu_reg_byte_123 ();  // open: out_8, in_2, h, v, in_1, out_7, s, e
  cpu_reg_byte cpu_reg_byte_124 ();  // open: out_8, in_2, h, v, in_1, out_7, s, e
  cpu_reg_byte cpu_reg_byte_125 ();  // open: out_8, in_2, h, v, in_1, out_7, s, e
  cpu_reg_byte cpu_reg_byte_126 ();  // open: out_8, in_2, h, v, in_1, out_7, s, e
  cpu_reg_byte cpu_reg_byte_127 ();  // open: out_8, in_2, h, v, in_1, out_7, s, e
  cpu_reg_byte cpu_reg_byte_128 ();  // open: out_8, in_2, h, v, in_1, out_7, s, e
  cpu_reg_byte cpu_reg_byte_129 (
    .in_2(reset), .h(cpu_decoder_4x16_1_out_2), .v(cpu_decoder_4x16_2_out_9), .in_1(\input ),
    .out_7(cpu_reg_byte_1_out_7), .s(s), .e(e));  // open: out_8
  cpu_reg_byte cpu_reg_byte_130 ();  // open: out_8, in_2, h, v, in_1, out_7, s, e
  cpu_reg_byte cpu_reg_byte_131 ();  // open: out_8, in_2, h, v, in_1, out_7, s, e
  cpu_reg_byte cpu_reg_byte_132 ();  // open: out_8, in_2, h, v, in_1, out_7, s, e
  cpu_reg_byte cpu_reg_byte_133 ();  // open: out_8, in_2, h, v, in_1, out_7, s, e
  cpu_reg_byte cpu_reg_byte_134 ();  // open: out_8, in_2, h, v, in_1, out_7, s, e
  cpu_reg_byte cpu_reg_byte_135 ();  // open: out_8, in_2, h, v, in_1, out_7, s, e
  cpu_reg_byte cpu_reg_byte_136 ();  // open: out_8, in_2, h, v, in_1, out_7, s, e
  cpu_reg_byte cpu_reg_byte_137 ();  // open: out_8, in_2, h, v, in_1, out_7, s, e
  cpu_reg_byte cpu_reg_byte_138 ();  // open: out_8, in_2, h, v, in_1, out_7, s, e
  cpu_reg_byte cpu_reg_byte_139 ();  // open: out_8, in_2, h, v, in_1, out_7, s, e
  cpu_reg_byte cpu_reg_byte_140 ();  // open: out_8, in_2, h, v, in_1, out_7, s, e
  cpu_reg_byte cpu_reg_byte_141 ();  // open: out_8, in_2, h, v, in_1, out_7, s, e
  cpu_reg_byte cpu_reg_byte_142 ();  // open: out_8, in_2, h, v, in_1, out_7, s, e
  cpu_reg_byte cpu_reg_byte_143 ();  // open: out_8, in_2, h, v, in_1, out_7, s, e
  cpu_reg_byte cpu_reg_byte_144 ();  // open: out_8, in_2, h, v, in_1, out_7, s, e
  cpu_reg_byte cpu_reg_byte_145 (
    .in_2(reset), .h(cpu_decoder_4x16_1_out_2), .v(cpu_decoder_4x16_2_out_8), .in_1(\input ),
    .out_7(cpu_reg_byte_1_out_7), .s(s), .e(e));  // open: out_8
  cpu_reg_byte cpu_reg_byte_146 ();  // open: out_8, in_2, h, v, in_1, out_7, s, e
  cpu_reg_byte cpu_reg_byte_147 ();  // open: out_8, in_2, h, v, in_1, out_7, s, e
  cpu_reg_byte cpu_reg_byte_148 ();  // open: out_8, in_2, h, v, in_1, out_7, s, e
  cpu_reg_byte cpu_reg_byte_149 ();  // open: out_8, in_2, h, v, in_1, out_7, s, e
  cpu_reg_byte cpu_reg_byte_150 ();  // open: out_8, in_2, h, v, in_1, out_7, s, e
  cpu_reg_byte cpu_reg_byte_151 ();  // open: out_8, in_2, h, v, in_1, out_7, s, e
  cpu_reg_byte cpu_reg_byte_152 ();  // open: out_8, in_2, h, v, in_1, out_7, s, e
  cpu_reg_byte cpu_reg_byte_153 ();  // open: out_8, in_2, h, v, in_1, out_7, s, e
  cpu_reg_byte cpu_reg_byte_154 ();  // open: out_8, in_2, h, v, in_1, out_7, s, e
  cpu_reg_byte cpu_reg_byte_155 ();  // open: out_8, in_2, h, v, in_1, out_7, s, e
  cpu_reg_byte cpu_reg_byte_156 ();  // open: out_8, in_2, h, v, in_1, out_7, s, e
  cpu_reg_byte cpu_reg_byte_157 ();  // open: out_8, in_2, h, v, in_1, out_7, s, e
  cpu_reg_byte cpu_reg_byte_158 ();  // open: out_8, in_2, h, v, in_1, out_7, s, e
  cpu_reg_byte cpu_reg_byte_159 ();  // open: out_8, in_2, h, v, in_1, out_7, s, e
  cpu_reg_byte cpu_reg_byte_160 ();  // open: out_8, in_2, h, v, in_1, out_7, s, e
  cpu_reg_byte cpu_reg_byte_161 (
    .in_2(reset), .h(cpu_decoder_4x16_1_out_2), .v(cpu_decoder_4x16_2_out_7), .in_1(\input ),
    .out_7(cpu_reg_byte_1_out_7), .s(s), .e(e));  // open: out_8
  cpu_reg_byte cpu_reg_byte_162 ();  // open: out_8, in_2, h, v, in_1, out_7, s, e
  cpu_reg_byte cpu_reg_byte_163 ();  // open: out_8, in_2, h, v, in_1, out_7, s, e
  cpu_reg_byte cpu_reg_byte_164 ();  // open: out_8, in_2, h, v, in_1, out_7, s, e
  cpu_reg_byte cpu_reg_byte_165 ();  // open: out_8, in_2, h, v, in_1, out_7, s, e
  cpu_reg_byte cpu_reg_byte_166 ();  // open: out_8, in_2, h, v, in_1, out_7, s, e
  cpu_reg_byte cpu_reg_byte_167 ();  // open: out_8, in_2, h, v, in_1, out_7, s, e
  cpu_reg_byte cpu_reg_byte_168 ();  // open: out_8, in_2, h, v, in_1, out_7, s, e
  cpu_reg_byte cpu_reg_byte_169 ();  // open: out_8, in_2, h, v, in_1, out_7, s, e
  cpu_reg_byte cpu_reg_byte_170 ();  // open: out_8, in_2, h, v, in_1, out_7, s, e
  cpu_reg_byte cpu_reg_byte_171 ();  // open: out_8, in_2, h, v, in_1, out_7, s, e
  cpu_reg_byte cpu_reg_byte_172 ();  // open: out_8, in_2, h, v, in_1, out_7, s, e
  cpu_reg_byte cpu_reg_byte_173 ();  // open: out_8, in_2, h, v, in_1, out_7, s, e
  cpu_reg_byte cpu_reg_byte_174 ();  // open: out_8, in_2, h, v, in_1, out_7, s, e
  cpu_reg_byte cpu_reg_byte_175 ();  // open: out_8, in_2, h, v, in_1, out_7, s, e
  cpu_reg_byte cpu_reg_byte_176 ();  // open: out_8, in_2, h, v, in_1, out_7, s, e
  cpu_reg_byte cpu_reg_byte_177 (
    .in_2(reset), .h(cpu_decoder_4x16_1_out_2), .v(cpu_decoder_4x16_2_out_6), .in_1(\input ),
    .out_7(cpu_reg_byte_1_out_7), .s(s), .e(e));  // open: out_8
  cpu_reg_byte cpu_reg_byte_178 ();  // open: out_8, in_2, h, v, in_1, out_7, s, e
  cpu_reg_byte cpu_reg_byte_179 ();  // open: out_8, in_2, h, v, in_1, out_7, s, e
  cpu_reg_byte cpu_reg_byte_180 ();  // open: out_8, in_2, h, v, in_1, out_7, s, e
  cpu_reg_byte cpu_reg_byte_181 ();  // open: out_8, in_2, h, v, in_1, out_7, s, e
  cpu_reg_byte cpu_reg_byte_182 ();  // open: out_8, in_2, h, v, in_1, out_7, s, e
  cpu_reg_byte cpu_reg_byte_183 ();  // open: out_8, in_2, h, v, in_1, out_7, s, e
  cpu_reg_byte cpu_reg_byte_184 ();  // open: out_8, in_2, h, v, in_1, out_7, s, e
  cpu_reg_byte cpu_reg_byte_185 ();  // open: out_8, in_2, h, v, in_1, out_7, s, e
  cpu_reg_byte cpu_reg_byte_186 ();  // open: out_8, in_2, h, v, in_1, out_7, s, e
  cpu_reg_byte cpu_reg_byte_187 ();  // open: out_8, in_2, h, v, in_1, out_7, s, e
  cpu_reg_byte cpu_reg_byte_188 ();  // open: out_8, in_2, h, v, in_1, out_7, s, e
  cpu_reg_byte cpu_reg_byte_189 ();  // open: out_8, in_2, h, v, in_1, out_7, s, e
  cpu_reg_byte cpu_reg_byte_190 ();  // open: out_8, in_2, h, v, in_1, out_7, s, e
  cpu_reg_byte cpu_reg_byte_191 ();  // open: out_8, in_2, h, v, in_1, out_7, s, e
  cpu_reg_byte cpu_reg_byte_192 ();  // open: out_8, in_2, h, v, in_1, out_7, s, e
  cpu_reg_byte cpu_reg_byte_193 (
    .in_2(reset), .h(cpu_decoder_4x16_1_out_2), .v(cpu_decoder_4x16_2_out_5), .in_1(\input ),
    .out_7(cpu_reg_byte_1_out_7), .s(s), .e(e));  // open: out_8
  cpu_reg_byte cpu_reg_byte_194 ();  // open: out_8, in_2, h, v, in_1, out_7, s, e
  cpu_reg_byte cpu_reg_byte_195 ();  // open: out_8, in_2, h, v, in_1, out_7, s, e
  cpu_reg_byte cpu_reg_byte_196 ();  // open: out_8, in_2, h, v, in_1, out_7, s, e
  cpu_reg_byte cpu_reg_byte_197 ();  // open: out_8, in_2, h, v, in_1, out_7, s, e
  cpu_reg_byte cpu_reg_byte_198 ();  // open: out_8, in_2, h, v, in_1, out_7, s, e
  cpu_reg_byte cpu_reg_byte_199 ();  // open: out_8, in_2, h, v, in_1, out_7, s, e
  cpu_reg_byte cpu_reg_byte_200 ();  // open: out_8, in_2, h, v, in_1, out_7, s, e
  cpu_reg_byte cpu_reg_byte_201 ();  // open: out_8, in_2, h, v, in_1, out_7, s, e
  cpu_reg_byte cpu_reg_byte_202 ();  // open: out_8, in_2, h, v, in_1, out_7, s, e
  cpu_reg_byte cpu_reg_byte_203 ();  // open: out_8, in_2, h, v, in_1, out_7, s, e
  cpu_reg_byte cpu_reg_byte_204 ();  // open: out_8, in_2, h, v, in_1, out_7, s, e
  cpu_reg_byte cpu_reg_byte_205 ();  // open: out_8, in_2, h, v, in_1, out_7, s, e
  cpu_reg_byte cpu_reg_byte_206 ();  // open: out_8, in_2, h, v, in_1, out_7, s, e
  cpu_reg_byte cpu_reg_byte_207 ();  // open: out_8, in_2, h, v, in_1, out_7, s, e
  cpu_reg_byte cpu_reg_byte_208 ();  // open: out_8, in_2, h, v, in_1, out_7, s, e
  cpu_reg_byte cpu_reg_byte_209 (
    .in_2(reset), .h(cpu_decoder_4x16_1_out_2), .v(cpu_decoder_4x16_2_out_4), .in_1(\input ),
    .out_7(cpu_reg_byte_1_out_7), .s(s), .e(e));  // open: out_8
  cpu_reg_byte cpu_reg_byte_210 ();  // open: out_8, in_2, h, v, in_1, out_7, s, e
  cpu_reg_byte cpu_reg_byte_211 ();  // open: out_8, in_2, h, v, in_1, out_7, s, e
  cpu_reg_byte cpu_reg_byte_212 ();  // open: out_8, in_2, h, v, in_1, out_7, s, e
  cpu_reg_byte cpu_reg_byte_213 ();  // open: out_8, in_2, h, v, in_1, out_7, s, e
  cpu_reg_byte cpu_reg_byte_214 ();  // open: out_8, in_2, h, v, in_1, out_7, s, e
  cpu_reg_byte cpu_reg_byte_215 ();  // open: out_8, in_2, h, v, in_1, out_7, s, e
  cpu_reg_byte cpu_reg_byte_216 ();  // open: out_8, in_2, h, v, in_1, out_7, s, e
  cpu_reg_byte cpu_reg_byte_217 ();  // open: out_8, in_2, h, v, in_1, out_7, s, e
  cpu_reg_byte cpu_reg_byte_218 ();  // open: out_8, in_2, h, v, in_1, out_7, s, e
  cpu_reg_byte cpu_reg_byte_219 ();  // open: out_8, in_2, h, v, in_1, out_7, s, e
  cpu_reg_byte cpu_reg_byte_220 ();  // open: out_8, in_2, h, v, in_1, out_7, s, e
  cpu_reg_byte cpu_reg_byte_221 ();  // open: out_8, in_2, h, v, in_1, out_7, s, e
  cpu_reg_byte cpu_reg_byte_222 ();  // open: out_8, in_2, h, v, in_1, out_7, s, e
  cpu_reg_byte cpu_reg_byte_223 ();  // open: out_8, in_2, h, v, in_1, out_7, s, e
  cpu_reg_byte cpu_reg_byte_224 ();  // open: out_8, in_2, h, v, in_1, out_7, s, e
  cpu_reg_byte cpu_reg_byte_225 (
    .in_2(reset), .h(cpu_decoder_4x16_1_out_2), .v(cpu_decoder_4x16_2_out_3), .in_1(\input ),
    .out_7(cpu_reg_byte_1_out_7), .s(s), .e(e));  // open: out_8
  cpu_reg_byte cpu_reg_byte_226 ();  // open: out_8, in_2, h, v, in_1, out_7, s, e
  cpu_reg_byte cpu_reg_byte_227 ();  // open: out_8, in_2, h, v, in_1, out_7, s, e
  cpu_reg_byte cpu_reg_byte_228 ();  // open: out_8, in_2, h, v, in_1, out_7, s, e
  cpu_reg_byte cpu_reg_byte_229 ();  // open: out_8, in_2, h, v, in_1, out_7, s, e
  cpu_reg_byte cpu_reg_byte_230 ();  // open: out_8, in_2, h, v, in_1, out_7, s, e
  cpu_reg_byte cpu_reg_byte_231 ();  // open: out_8, in_2, h, v, in_1, out_7, s, e
  cpu_reg_byte cpu_reg_byte_232 ();  // open: out_8, in_2, h, v, in_1, out_7, s, e
  cpu_reg_byte cpu_reg_byte_233 ();  // open: out_8, in_2, h, v, in_1, out_7, s, e
  cpu_reg_byte cpu_reg_byte_234 ();  // open: out_8, in_2, h, v, in_1, out_7, s, e
  cpu_reg_byte cpu_reg_byte_235 ();  // open: out_8, in_2, h, v, in_1, out_7, s, e
  cpu_reg_byte cpu_reg_byte_236 ();  // open: out_8, in_2, h, v, in_1, out_7, s, e
  cpu_reg_byte cpu_reg_byte_237 ();  // open: out_8, in_2, h, v, in_1, out_7, s, e
  cpu_reg_byte cpu_reg_byte_238 ();  // open: out_8, in_2, h, v, in_1, out_7, s, e
  cpu_reg_byte cpu_reg_byte_239 ();  // open: out_8, in_2, h, v, in_1, out_7, s, e
  cpu_reg_byte cpu_reg_byte_240 ();  // open: out_8, in_2, h, v, in_1, out_7, s, e
  cpu_reg_byte cpu_reg_byte_241 (
    .in_2(reset), .h(cpu_decoder_4x16_1_out_2), .v(cpu_decoder_4x16_2_out_2), .in_1(\input ),
    .out_7(cpu_reg_byte_1_out_7), .s(s), .e(e));  // open: out_8
  cpu_reg_byte cpu_reg_byte_242 ();  // open: out_8, in_2, h, v, in_1, out_7, s, e
  cpu_reg_byte cpu_reg_byte_243 ();  // open: out_8, in_2, h, v, in_1, out_7, s, e
  cpu_reg_byte cpu_reg_byte_244 ();  // open: out_8, in_2, h, v, in_1, out_7, s, e
  cpu_reg_byte cpu_reg_byte_245 ();  // open: out_8, in_2, h, v, in_1, out_7, s, e
  cpu_reg_byte cpu_reg_byte_246 ();  // open: out_8, in_2, h, v, in_1, out_7, s, e
  cpu_reg_byte cpu_reg_byte_247 ();  // open: out_8, in_2, h, v, in_1, out_7, s, e
  cpu_reg_byte cpu_reg_byte_248 ();  // open: out_8, in_2, h, v, in_1, out_7, s, e
  cpu_reg_byte cpu_reg_byte_249 ();  // open: out_8, in_2, h, v, in_1, out_7, s, e
  cpu_reg_byte cpu_reg_byte_250 ();  // open: out_8, in_2, h, v, in_1, out_7, s, e
  cpu_reg_byte cpu_reg_byte_251 ();  // open: out_8, in_2, h, v, in_1, out_7, s, e
  cpu_reg_byte cpu_reg_byte_252 ();  // open: out_8, in_2, h, v, in_1, out_7, s, e
  cpu_reg_byte cpu_reg_byte_253 ();  // open: out_8, in_2, h, v, in_1, out_7, s, e
  cpu_reg_byte cpu_reg_byte_254 ();  // open: out_8, in_2, h, v, in_1, out_7, s, e
  cpu_reg_byte cpu_reg_byte_255 ();  // open: out_8, in_2, h, v, in_1, out_7, s, e
  cpu_reg_byte cpu_reg_byte_256 ();  // open: out_8, in_2, h, v, in_1, out_7, s, e
endmodule

module cpu_alu (
  input  [7:0] a,
  input  [7:0] b,
  input  carry_in,
  input  a_2,
  input  b_2,
  input  c,
  output a_large,
  output equal,
  output zero,
  output [7:0] c_2,
  output carry_out
);

  wire adder_1_cout, and_2_out, and_3_out, and_4_out, cpu_decoder_3x8_1_out_2, cpu_decoder_3x8_1_out_3,
       cpu_decoder_3x8_1_out_4, cpu_decoder_3x8_1_out_5, cpu_decoder_3x8_1_out_6, cpu_decoder_3x8_1_out_7,
       cpu_decoder_3x8_1_out_8, cpu_shl_1_shift_out, cpu_shr_1_shift_out, or_2_out;
  wire [7:0] adder_1_out, and_1_out, cpu_shl_1_o, cpu_shr_1_o, cpu_xor_le_8_1_out_3, not_1_out, or_1_out;

  assign or_1_out = a | b;  // OR_Gate or_1, 8 bits wide
  assign and_1_out = a & b;  // AND_Gate and_1, 8 bits wide
  assign not_1_out = ~a;  // NOT_Gate not_1, 8 bits wide
  cpu_shl cpu_shl_1 (.shift_in(carry_in), .i(a), .o(cpu_shl_1_o), .shift_out(cpu_shl_1_shift_out));
  cpu_shr cpu_shr_1 (.shift_out(cpu_shr_1_shift_out), .i(a), .shift_in(carry_in), .o(cpu_shr_1_o));
  Adder adder_1 (.a(a), .b(b), .out(adder_1_out), .cin(carry_in), .cout(adder_1_cout));
  cpu_xor_le_8 cpu_xor_le_8_1 (.a(a), .b(b), .out_3(cpu_xor_le_8_1_out_3), .a_large(a_large), .equal(equal));
  cpu_decoder_3x8 cpu_decoder_3x8_1 (
    .in_1({c, b_2, a_2}), .out_2(cpu_decoder_3x8_1_out_2), .out_3(cpu_decoder_3x8_1_out_3),
    .out_4(cpu_decoder_3x8_1_out_4), .out_5(cpu_decoder_3x8_1_out_5), .out_6(cpu_decoder_3x8_1_out_6),
    .out_7(cpu_decoder_3x8_1_out_7), .out_8(cpu_decoder_3x8_1_out_8));  // open: out_9
  cpu_e cpu_e_1 (.in_1(cpu_xor_le_8_1_out_3), .out_3(c_2), .in_2(cpu_decoder_3x8_1_out_8));
  cpu_e cpu_e_2 (.in_1(or_1_out), .out_3(c_2), .in_2(cpu_decoder_3x8_1_out_7));
  cpu_e cpu_e_3 (.in_1(and_1_out), .out_3(c_2), .in_2(cpu_decoder_3x8_1_out_6));
  cpu_e cpu_e_4 (.in_1(not_1_out), .out_3(c_2), .in_2(cpu_decoder_3x8_1_out_5));
  cpu_e cpu_e_5 (.in_1(adder_1_out), .out_3(c_2), .in_2(cpu_decoder_3x8_1_out_2));
  cpu_e cpu_e_6 (.in_1(cpu_shl_1_o), .out_3(c_2), .in_2(cpu_decoder_3x8_1_out_4));
  and and_2 (and_2_out, cpu_shl_1_shift_out, cpu_decoder_3x8_1_out_4);
  cpu_e cpu_e_7 (.in_1(cpu_shr_1_o), .out_3(c_2), .in_2(cpu_decoder_3x8_1_out_3));
  and and_3 (and_3_out, cpu_shr_1_shift_out, cpu_decoder_3x8_1_out_3);
  and and_4 (and_4_out, adder_1_cout, cpu_decoder_3x8_1_out_2);
  assign carry_out = cpu_decoder_3x8_1_out_4 ? and_2_out : 1'bz;  // Controlled_Buffer controlled_buffer_1
  assign carry_out = cpu_decoder_3x8_1_out_3 ? and_3_out : 1'bz;  // Controlled_Buffer controlled_buffer_2
  assign carry_out = cpu_decoder_3x8_1_out_2 ? and_4_out : 1'bz;  // Controlled_Buffer controlled_buffer_3
  or or_2 (or_2_out, c_2[0], c_2[1], c_2[2], c_2[3], c_2[4], c_2[5], c_2[6], c_2[7]);
  not not_2 (zero, or_2_out);
endmodule

module cpu_e (
  input  [7:0] in_1,
  input  in_2,
  output [7:0] out_3
);

  wire and_1_out, and_2_out, and_3_out, and_4_out, and_5_out, and_6_out, and_7_out, and_8_out;

  and and_1 (and_1_out, in_1[0], in_2);
  and and_2 (and_2_out, in_1[1], in_2);
  and and_3 (and_3_out, in_1[2], in_2);
  and and_4 (and_4_out, in_1[3], in_2);
  and and_5 (and_5_out, in_1[4], in_2);
  and and_6 (and_6_out, in_1[5], in_2);
  and and_7 (and_7_out, in_1[6], in_2);
  and and_8 (and_8_out, in_1[7], in_2);
  assign out_3[0] = in_2 ? and_1_out : 1'bz;  // Controlled_Buffer controlled_buffer_1
  assign out_3[1] = in_2 ? and_2_out : 1'bz;  // Controlled_Buffer controlled_buffer_2
  assign out_3[2] = in_2 ? and_3_out : 1'bz;  // Controlled_Buffer controlled_buffer_3
  assign out_3[3] = in_2 ? and_4_out : 1'bz;  // Controlled_Buffer controlled_buffer_4
  assign out_3[4] = in_2 ? and_5_out : 1'bz;  // Controlled_Buffer controlled_buffer_5
  assign out_3[5] = in_2 ? and_6_out : 1'bz;  // Controlled_Buffer controlled_buffer_6
  assign out_3[6] = in_2 ? and_7_out : 1'bz;  // Controlled_Buffer controlled_buffer_7
  assign out_3[7] = in_2 ? and_8_out : 1'bz;  // Controlled_Buffer controlled_buffer_8
endmodule

module cpu_shr (
  input  [7:0] i,
  input  shift_in,
  output shift_out,
  output [7:0] o
);


  assign o = {shift_in, i[7:1]};
  assign shift_out = i[0];
endmodule

module cpu_shl (
  input  shift_in,
  input  [7:0] i,
  output [7:0] o,
  output shift_out
);


  assign o = {i[6:0], shift_in};
  assign shift_out = i[7];
endmodule

module cpu_xor_le_1 (
  input  above_equal,
  input  a_larger,
  input  a,
  input  b,
  output c,
  output a_large,
  output equal
);

  wire and_2_out, not_1_out;

  xor xor_1 (c, a, b);
  not not_1 (not_1_out, c);
  and and_1 (equal, not_1_out, above_equal);
  and and_2 (and_2_out, above_equal, a, c);
  or or_1 (a_large, and_2_out, a_larger);
endmodule

module cpu_xor_le_8 (
  input  [7:0] a,
  input  [7:0] b,
  output [7:0] out_3,
  output a_large,
  output equal
);

  wire cpu_xor_le_1_1_a_large, cpu_xor_le_1_1_equal, cpu_xor_le_1_2_a_large, cpu_xor_le_1_2_equal,
       cpu_xor_le_1_3_a_large, cpu_xor_le_1_3_equal, cpu_xor_le_1_4_a_large, cpu_xor_le_1_4_equal,
       cpu_xor_le_1_5_a_large, cpu_xor_le_1_5_equal, cpu_xor_le_1_6_a_large, cpu_xor_le_1_6_equal,
       cpu_xor_le_1_7_a_large, cpu_xor_le_1_7_equal;

  cpu_xor_le_1 cpu_xor_le_1_1 (
    .a(a[0]), .b(b[0]), .c(out_3[0]), .above_equal(1'b1), .a_larger(1'b0), .equal(cpu_xor_le_1_1_equal),
    .a_large(cpu_xor_le_1_1_a_large));
  cpu_xor_le_1 cpu_xor_le_1_2 (
    .a(a[1]), .b(b[1]), .c(out_3[1]), .above_equal(cpu_xor_le_1_1_equal), .a_larger(cpu_xor_le_1_1_a_large),
    .equal(cpu_xor_le_1_2_equal), .a_large(cpu_xor_le_1_2_a_large));
  cpu_xor_le_1 cpu_xor_le_1_3 (
    .a(a[2]), .b(b[2]), .c(out_3[2]), .above_equal(cpu_xor_le_1_2_equal), .a_larger(cpu_xor_le_1_2_a_large),
    .equal(cpu_xor_le_1_3_equal), .a_large(cpu_xor_le_1_3_a_large));
  cpu_xor_le_1 cpu_xor_le_1_4 (
    .a(a[3]), .b(b[3]), .c(out_3[3]), .above_equal(cpu_xor_le_1_3_equal), .a_larger(cpu_xor_le_1_3_a_large),
    .equal(cpu_xor_le_1_4_equal), .a_large(cpu_xor_le_1_4_a_large));
  cpu_xor_le_1 cpu_xor_le_1_5 (
    .a(a[4]), .b(b[4]), .c(out_3[4]), .above_equal(cpu_xor_le_1_4_equal), .a_larger(cpu_xor_le_1_4_a_large),
    .equal(cpu_xor_le_1_5_equal), .a_large(cpu_xor_le_1_5_a_large));
  cpu_xor_le_1 cpu_xor_le_1_6 (
    .a(a[5]), .b(b[5]), .c(out_3[5]), .above_equal(cpu_xor_le_1_5_equal), .a_larger(cpu_xor_le_1_5_a_large),
    .equal(cpu_xor_le_1_6_equal), .a_large(cpu_xor_le_1_6_a_large));
  cpu_xor_le_1 cpu_xor_le_1_7 (
    .a(a[6]), .b(b[6]), .c(out_3[6]), .above_equal(cpu_xor_le_1_6_equal), .a_larger(cpu_xor_le_1_6_a_large),
    .equal(cpu_xor_le_1_7_equal), .a_large(cpu_xor_le_1_7_a_large));
  cpu_xor_le_1 cpu_xor_le_1_8 (
    .a(a[7]), .b(b[7]), .c(out_3[7]), .above_equal(cpu_xor_le_1_7_equal), .a_larger(cpu_xor_le_1_7_a_large),
    .equal(equal), .a_large(a_large));
endmodule

module cpu_bus_1 (
  input  [7:0] in_1,
  input  bus_1,
  output [7:0] out_3
);

  wire not_1_out;

  and and_1 (out_3[7], in_1[7], not_1_out);
  and and_2 (out_3[6], in_1[6], not_1_out);
  and and_3 (out_3[5], in_1[5], not_1_out);
  and and_4 (out_3[4], in_1[4], not_1_out);
  and and_5 (out_3[3], in_1[3], not_1_out);
  and and_6 (out_3[2], in_1[2], not_1_out);
  and and_7 (out_3[1], in_1[1], not_1_out);
  not not_1 (not_1_out, bus_1);
  or or_1 (out_3[0], in_1[0], bus_1);
endmodule

module cpu (
  input  in_1,
  input  in_2,
  input  in_3,
  input  in_4,
  input  [7:0] in_5,
  output [7:0] out_6,
  output [7:0] out_7,
  output [7:0] out_8,
  output [7:0] out_9,
  output [7:0] out_10,
  output [7:0] out_11
);

  wire CLK_out, cpu_clk_1_clk, cpu_clk_1_clk_e, cpu_clk_1_clk_s, cpu_control_section_1_acc_e,
       cpu_control_section_1_acc_s, cpu_control_section_1_bus_1, cpu_control_section_1_iar_e,
       cpu_control_section_1_iar_s, cpu_control_section_1_ir_s, cpu_control_section_1_mar_s,
       cpu_control_section_1_r0_e, cpu_control_section_1_r0_s, cpu_control_section_1_r1_e,
       cpu_control_section_1_r1_s, cpu_control_section_1_r2_e, cpu_control_section_1_r2_s,
       cpu_control_section_1_r3_e, cpu_control_section_1_r3_s, cpu_control_section_1_ram_e,
       cpu_control_section_1_ram_s, cpu_control_section_1_tmp_s;
  wire [7:0] controlled_buffer_1_out, cpu_alu_1_c_2, cpu_bus_1_1_out_3, cpu_ir_1_output,
       cpu_register_8_1_out_5, cpu_temp_1_out_3;

  assign controlled_buffer_1_out = in_4 ? in_5 : 8'bz;  // Controlled_Buffer controlled_buffer_1
  cpu_temp cpu_temp_1 (
    .in_1({cpu_register_8_1_out_5[7:5], cpu_register_8_1_out_5[5], cpu_register_8_1_out_5[3:0]}),
    .out_3(cpu_temp_1_out_3), .in_2(cpu_control_section_1_tmp_s));
  cpu_alu cpu_alu_1 (
    .a({cpu_register_8_1_out_5[7:5], cpu_register_8_1_out_5[5], cpu_register_8_1_out_5[3:0]}),
    .b(cpu_bus_1_1_out_3), .a_2(in_1), .b_2(in_2), .c(in_3), .c_2(cpu_alu_1_c_2));  // open: carry_in, a_large, equal, zero, carry_out
  cpu_register_8 cpu_register_8_1 (
    .in_1(cpu_alu_1_c_2),
    .out_5({cpu_register_8_1_out_5[7:5], cpu_register_8_1_out_5[5], cpu_register_8_1_out_5[3:0]}),
    .s(cpu_control_section_1_acc_s), .e(cpu_control_section_1_acc_e), .out_4(out_10));
  cpu_bus_1 cpu_bus_1_1 (.in_1(cpu_temp_1_out_3), .out_3(cpu_bus_1_1_out_3), .bus_1(cpu_control_section_1_bus_1));
  Clock CLK (.out(CLK_out));
  cpu_clk cpu_clk_1 (.clk_in(CLK_out), .clk(cpu_clk_1_clk), .clk_s(cpu_clk_1_clk_s), .clk_e(cpu_clk_1_clk_e));
  cpu_register_8 cpu_register_8_2 (
    .in_1({cpu_register_8_1_out_5[7:5], cpu_register_8_1_out_5[5], cpu_register_8_1_out_5[3:0]}),
    .out_5({cpu_register_8_1_out_5[7:5], cpu_register_8_1_out_5[5], cpu_register_8_1_out_5[3:0]}),
    .s(cpu_control_section_1_r0_s), .e(cpu_control_section_1_r0_e), .out_4(out_7));
  cpu_register_8 cpu_register_8_3 (
    .in_1({cpu_register_8_1_out_5[7:5], cpu_register_8_1_out_5[5], cpu_register_8_1_out_5[3:0]}),
    .out_5({cpu_register_8_1_out_5[7:5], cpu_register_8_1_out_5[5], cpu_register_8_1_out_5[3:0]}),
    .s(cpu_control_section_1_r1_s), .e(cpu_control_section_1_r1_e), .out_4(out_8));
  cpu_iar cpu_iar_1 (
    .out_4(out_11),
    .in_1({cpu_register_8_1_out_5[7:5], cpu_register_8_1_out_5[5], cpu_register_8_1_out_5[3:0]}),
    .out_5({cpu_register_8_1_out_5[7:5], cpu_register_8_1_out_5[5], cpu_register_8_1_out_5[3:0]}),
    .in_2(cpu_control_section_1_iar_s), .in_3(cpu_control_section_1_iar_e));
  cpu_ir cpu_ir_1 (
    .\input ({cpu_register_8_1_out_5[7:5], cpu_register_8_1_out_5[5], cpu_register_8_1_out_5[3:0]}),
    .\output (cpu_ir_1_output), .in_2(cpu_control_section_1_ir_s));
  cpu_control_section cpu_control_section_1 (
    .clk(cpu_clk_1_clk), .clk_s(cpu_clk_1_clk_s), .clk_e(cpu_clk_1_clk_e),
    .RAM_e(cpu_control_section_1_ram_e), .ACC_e(cpu_control_section_1_acc_e),
    .R0_e(cpu_control_section_1_r0_e), .R1_e(cpu_control_section_1_r1_e), .R2_e(cpu_control_section_1_r2_e),
    .R3_e(cpu_control_section_1_r3_e), .MAR_s(cpu_control_section_1_mar_s),
    .ACC_s(cpu_control_section_1_acc_s), .RAM_s(cpu_control_section_1_ram_s),
    .TMP_s(cpu_control_section_1_tmp_s), .R0_s(cpu_control_section_1_r0_s),
    .R1_s(cpu_control_section_1_r1_s), .R2_s(cpu_control_section_1_r2_s), .R3_s(cpu_control_section_1_r3_s),
    .IR_in(cpu_ir_1_output), .IR_s(cpu_control_section_1_ir_s), .IAR_e(cpu_control_section_1_iar_e),
    .IAR_s(cpu_control_section_1_iar_s), .bus_1(cpu_control_section_1_bus_1));  // open: out_23, out_24, out_25
  cpu_register_8 cpu_register_8_4 (
    .in_1({cpu_register_8_1_out_5[7:5], cpu_register_8_1_out_5[5], cpu_register_8_1_out_5[3:0]}),
    .out_5({cpu_register_8_1_out_5[7:5], cpu_register_8_1_out_5[5], cpu_register_8_1_out_5[3:0]}),
    .s(cpu_control_section_1_r2_s), .e(cpu_control_section_1_r2_e), .out_4(out_6));
  cpu_ram_my_version cpu_ram_my_version_1 (
    .address({cpu_register_8_1_out_5[7:5], cpu_register_8_1_out_5[5], cpu_register_8_1_out_5[3:0]}),
    .\input ({cpu_register_8_1_out_5[7:5], cpu_register_8_1_out_5[5], cpu_register_8_1_out_5[3:0]}),
    .s(cpu_control_section_1_ram_s), .e(cpu_control_section_1_ram_e),
    .\output ({cpu_register_8_1_out_5[7:5], cpu_register_8_1_out_5[5], cpu_register_8_1_out_5[3:0]}),
    .sa(cpu_control_section_1_mar_s));
  cpu_register_8 cpu_register_8_5 (
    .in_1({cpu_register_8_1_out_5[7:5], cpu_register_8_1_out_5[5], cpu_register_8_1_out_5[3:0]}),
    .out_5({cpu_register_8_1_out_5[7:5], cpu_register_8_1_out_5[5], cpu_register_8_1_out_5[3:0]}),
    .s(cpu_control_section_1_r3_s), .e(cpu_control_section_1_r3_e), .out_4(out_9));
endmodule

module cpu_control_section (
  input  clk,
  input  clk_s,
  input  clk_e,
  input  [7:0] IR_in,
  output IAR_s,
  output bus_1,
  output IR_s,
  output IAR_e,
  output MAR_s,
  output ACC_s,
  output RAM_e,
  output RAM_s,
  output ACC_e,
  output TMP_s,
  output R0_e,
  output R0_s,
  output R1_e,
  output R1_s,
  output R2_s,
  output R2_e,
  output R3_s,
  output R3_e,
  output out_23,
  output out_24,
  output out_25
);

  wire ACC_E_t, ACC_S_t, and_4_out, and_5_out, and_6_out, and_7_out, and_8_out, and_9_out, and_10_out,
       and_11_out, and_15_out, cpu_stepper_1__2, cpu_stepper_1__3, cpu_stepper_1__4, cpu_stepper_1__5,
       cpu_stepper_1__6, cpu_stepper_1__7, decoder_1_out0, decoder_1_out1, decoder_1_out2, decoder_1_out3,
       decoder_2_out0, decoder_2_out1, decoder_2_out2, decoder_2_out3, decoder_3_out0, decoder_3_out1,
       decoder_3_out2, decoder_3_out3, not_1_out, or_5_out, or_6_out, REG_B_E;

  or or_1 (R0_e, and_4_out, and_8_out);
  or or_2 (R1_e, and_5_out, and_9_out);
  or or_3 (R2_e, and_6_out, and_10_out);
  or or_4 (R3_e, and_7_out, and_11_out);
  and and_1 (IAR_e, bus_1, clk_e);
  and and_2 (RAM_e, clk_e, cpu_stepper_1__2);
  and and_3 (ACC_e, clk_e, or_5_out);
  and and_4 (and_4_out, clk_e, REG_B_E, decoder_1_out0);
  and and_5 (and_5_out, clk_e, REG_B_E, decoder_1_out1);
  and and_6 (and_6_out, clk_e, REG_B_E, decoder_1_out2);
  and and_7 (and_7_out, clk_e, REG_B_E, decoder_1_out3);
  and and_8 (and_8_out, clk_e, ACC_S_t, decoder_2_out0);
  and and_9 (and_9_out, clk_e, ACC_S_t, decoder_2_out1);
  and and_10 (and_10_out, clk_e, ACC_S_t, decoder_2_out2);
  and and_11 (and_11_out, clk_e, ACC_S_t, decoder_2_out3);
  and and_12 (out_23, cpu_stepper_1__5, IR_in[7], IR_in[4]);
  and and_13 (out_24, cpu_stepper_1__5, IR_in[7], IR_in[5]);
  and and_14 (out_25, cpu_stepper_1__5, IR_in[7], IR_in[6]);
  or or_5 (or_5_out, cpu_stepper_1__3, ACC_E_t);
  Decoder #(.select(2)) decoder_1 (
    .out0(decoder_1_out0), .out1(decoder_1_out1), .out2(decoder_1_out2), .out3(decoder_1_out3),
    .sel(IR_in[1:0]));  // open: en
  Decoder #(.select(2)) decoder_2 (
    .out0(decoder_2_out0), .out1(decoder_2_out1), .out2(decoder_2_out2), .out3(decoder_2_out3),
    .sel(IR_in[3:2]));  // open: en
  cpu_stepper cpu_stepper_1 (
    .clk(clk), ._1(bus_1), ._2(cpu_stepper_1__2), ._3(cpu_stepper_1__3), ._4(cpu_stepper_1__4),
    ._5(cpu_stepper_1__5), ._6(cpu_stepper_1__6), ._7(cpu_stepper_1__7), .reset(cpu_stepper_1__7));
  and and_15 (and_15_out, IR_in[4], IR_in[5], IR_in[6]);
  and and_16 (REG_B_E, cpu_stepper_1__4, IR_in[7]);
  not not_1 (not_1_out, and_15_out);
  and and_17 (ACC_S_t, cpu_stepper_1__5, IR_in[7]);
  and and_18 (ACC_E_t, cpu_stepper_1__6, IR_in[7], not_1_out);
  or or_6 (or_6_out, bus_1, ACC_S_t);
  Decoder #(.select(2)) decoder_3 (
    .out0(decoder_3_out0), .out1(decoder_3_out1), .out2(decoder_3_out2), .out3(decoder_3_out3),
    .sel(IR_in[1:0]));  // open: en
  and and_19 (IAR_s, cpu_stepper_1__3, clk_s);
  and and_20 (IR_s, cpu_stepper_1__2, clk_s);
  and and_21 (MAR_s, clk_s, bus_1);
  and and_22 (ACC_s, clk_s, or_6_out);
  and and_23 (RAM_s, clk_s, 1'b0);
  and and_24 (TMP_s, clk_s, REG_B_E);
  and and_25 (R0_s, clk_s, ACC_E_t, decoder_3_out0);
  and and_26 (R1_s, clk_s, ACC_E_t, decoder_3_out1);
  and and_27 (R2_s, clk_s, ACC_E_t, decoder_3_out2);
  and and_28 (R3_s, clk_s, ACC_E_t, decoder_3_out3);

  // Other names for the same wires on the sheet: REG_A_E = ACC_S_t; REG_B_S = ACC_E_t; TMP_S_t = REG_B_E

  // Notes on the sheet:
  //   reg b
  //   reg a
endmodule

module cpu_stepper (
  input  reset,
  input  clk,
  output _2,
  output _1,
  output _3,
  output _4,
  output _5,
  output _6,
  output _7
);

  wire cpu_memory_1_1_out_3, cpu_memory_1_2_out_3, cpu_memory_1_3_out_3, cpu_memory_1_4_out_3,
       cpu_memory_1_5_out_3, cpu_memory_1_6_out_3, cpu_memory_1_7_out_3, cpu_memory_1_8_out_3,
       cpu_memory_1_9_out_3, cpu_memory_1_10_out_3, cpu_memory_1_11_out_3, not_1_out, not_2_out, not_3_out,
       not_4_out, not_5_out, not_6_out, not_7_out, not_8_out, or_1_out, or_2_out;

  not not_1 (not_1_out, clk);
  not not_2 (not_2_out, reset);
  or or_1 (or_1_out, reset, clk);
  or or_2 (or_2_out, reset, not_1_out);
  cpu_memory_1 cpu_memory_1_1 (.in_1(not_2_out), .out_3(cpu_memory_1_1_out_3), .in_2(or_1_out));
  cpu_memory_1 cpu_memory_1_2 (.in_1(cpu_memory_1_1_out_3), .out_3(cpu_memory_1_2_out_3), .in_2(or_2_out));
  or or_3 (_1, reset, not_3_out);
  not not_3 (not_3_out, cpu_memory_1_2_out_3);
  cpu_memory_1 cpu_memory_1_3 (.in_1(cpu_memory_1_2_out_3), .out_3(cpu_memory_1_3_out_3), .in_2(or_1_out));
  cpu_memory_1 cpu_memory_1_4 (.in_1(cpu_memory_1_3_out_3), .out_3(cpu_memory_1_4_out_3), .in_2(or_2_out));
  and and_1 (_2, cpu_memory_1_2_out_3, not_4_out);
  not not_4 (not_4_out, cpu_memory_1_4_out_3);
  cpu_memory_1 cpu_memory_1_5 (.in_1(cpu_memory_1_4_out_3), .out_3(cpu_memory_1_5_out_3), .in_2(or_1_out));
  and and_2 (_3, cpu_memory_1_4_out_3, not_5_out);
  cpu_memory_1 cpu_memory_1_6 (.in_1(cpu_memory_1_5_out_3), .out_3(cpu_memory_1_6_out_3), .in_2(or_2_out));
  not not_5 (not_5_out, cpu_memory_1_6_out_3);
  cpu_memory_1 cpu_memory_1_7 (.in_1(cpu_memory_1_6_out_3), .out_3(cpu_memory_1_7_out_3), .in_2(or_1_out));
  and and_3 (_4, cpu_memory_1_6_out_3, not_6_out);
  not not_6 (not_6_out, cpu_memory_1_8_out_3);
  cpu_memory_1 cpu_memory_1_8 (.in_1(cpu_memory_1_7_out_3), .out_3(cpu_memory_1_8_out_3), .in_2(or_2_out));
  cpu_memory_1 cpu_memory_1_9 (.in_1(cpu_memory_1_8_out_3), .out_3(cpu_memory_1_9_out_3), .in_2(or_1_out));
  and and_4 (_5, cpu_memory_1_8_out_3, not_7_out);
  not not_7 (not_7_out, cpu_memory_1_10_out_3);
  cpu_memory_1 cpu_memory_1_10 (.in_1(cpu_memory_1_9_out_3), .out_3(cpu_memory_1_10_out_3), .in_2(or_2_out));
  and and_5 (_6, cpu_memory_1_10_out_3, not_8_out);
  cpu_memory_1 cpu_memory_1_11 (.in_1(cpu_memory_1_10_out_3), .out_3(cpu_memory_1_11_out_3), .in_2(or_1_out));
  not not_8 (not_8_out, _7);
  cpu_memory_1 cpu_memory_1_12 (.in_1(cpu_memory_1_11_out_3), .out_3(_7), .in_2(or_2_out));
endmodule

module cpu_clk (
  input  clk_in,
  output clk,
  output clk_s,
  output clk_e
);

  wire j_k_ff_1_qn, nand_1_out;

  J_K_Flip_Flop j_k_ff_1 (.J(1'b1), .clk(clk_in), .K(1'b1), .Q(clk), .Qn(j_k_ff_1_qn));  // open: preset, en, reset
  nand nand_1 (nand_1_out, clk_in, clk);
  nand nand_2 (clk_e, j_k_ff_1_qn, clk_in);
  not not_1 (clk_s, nand_1_out);
endmodule

module cpu_temp (
  input  [7:0] in_1,
  input  in_2,
  output [7:0] out_3
);

  wire [7:0] controlled_buffer_1_out;

  assign controlled_buffer_1_out = in_2 ? in_1 : 8'bz;  // Controlled_Buffer controlled_buffer_1
  cpu_mem_8 cpu_mem_8_1 (.in_1(controlled_buffer_1_out), .out_3(out_3), .in_2(in_2));
endmodule

module cpu_ram_my_version (
  input  [7:0] address,
  input  sa,
  input  [7:0] \input ,
  input  s,
  input  e,
  output [7:0] \output 
);

  wire [7:0] cpu_eneb_8_1_out_3, cpu_mem_8_1_out_3, ram_1_data;

  cpu_mem_8 cpu_mem_8_1 (.in_1(address), .out_3(cpu_mem_8_1_out_3), .in_2(sa));
  RAM #(.bus("separate")) ram_1 (
    .addr(cpu_mem_8_1_out_3), .din(\input ), .data(ram_1_data), .clk(s));  // open: str, sel, ld, clr
  cpu_eneb_8 cpu_eneb_8_1 (.in_1(ram_1_data), .out_3(cpu_eneb_8_1_out_3), .in_2(e));
  assign \output  = e ? cpu_eneb_8_1_out_3 : 8'bz;  // Controlled_Buffer controlled_buffer_1
endmodule

module cpu_ir (
  input  [7:0] \input ,
  input  in_2,
  output [7:0] \output 
);

  cpu_mem_8 cpu_mem_8_1 (.in_1(\input ), .out_3(\output ), .in_2(in_2));
endmodule

module cpu_iar (
  input  [7:0] in_1,
  input  in_2,
  input  in_3,
  output [7:0] out_4,
  output [7:0] out_5
);

  cpu_register_8 cpu_register_8_1 (.in_1(in_1), .out_5(out_5), .s(in_2), .e(in_3), .out_4(out_4));
endmodule
