// Logisim project logisim_evolution__version.circ as structural Verilog
module cpu_mem_1 (
  input  i,
  input  s,
  output o
);

  D_Flip_Flop #(.trigger("high")) d_ff_1 (.D(i), .clk(s), .Q(o));  // open: Qn, preset, reset

  // Notes on the sheet:
  //   s: initial=0x1
endmodule

module cpu_mem_8 (
  input  [7:0] i,
  input  s,
  output [7:0] out_3
);

  cpu_mem_1 cpu_mem_1_1 (.i(i[0]), .s(s), .o(out_3[0]));
  cpu_mem_1 cpu_mem_1_2 (.i(i[1]), .s(s), .o(out_3[1]));
  cpu_mem_1 cpu_mem_1_3 (.i(i[2]), .s(s), .o(out_3[2]));
  cpu_mem_1 cpu_mem_1_4 (.i(i[3]), .s(s), .o(out_3[3]));
  cpu_mem_1 cpu_mem_1_5 (.i(i[4]), .s(s), .o(out_3[4]));
  cpu_mem_1 cpu_mem_1_6 (.i(i[5]), .s(s), .o(out_3[5]));
  cpu_mem_1 cpu_mem_1_7 (.i(i[6]), .s(s), .o(out_3[6]));
  cpu_mem_1 cpu_mem_1_8 (.i(i[7]), .s(s), .o(out_3[7]));

  // Notes on the sheet:
  //   s: initial=0x1
endmodule

module cpu_eneb_8 (
  input  [7:0] i,
  input  e,
  output [7:0] o
);

  wire and_1_out, and_2_out, and_3_out, and_4_out, and_5_out, and_6_out, and_7_out, and_8_out;

  and and_1 (and_1_out, i[0], e);
  and and_2 (and_2_out, i[1], e);
  and and_3 (and_3_out, i[2], e);
  and and_4 (and_4_out, i[3], e);
  and and_5 (and_5_out, i[4], e);
  and and_6 (and_6_out, i[5], e);
  and and_7 (and_7_out, i[6], e);
  and and_8 (and_8_out, i[7], e);
  assign o[0] = e ? and_1_out : 1'bz;  // Controlled_Buffer controlled_buffer_1
  assign o[1] = e ? and_2_out : 1'bz;  // Controlled_Buffer controlled_buffer_2
  assign o[2] = e ? and_3_out : 1'bz;  // Controlled_Buffer controlled_buffer_3
  assign o[3] = e ? and_4_out : 1'bz;  // Controlled_Buffer controlled_buffer_4
  assign o[4] = e ? and_5_out : 1'bz;  // Controlled_Buffer controlled_buffer_5
  assign o[5] = e ? and_6_out : 1'bz;  // Controlled_Buffer controlled_buffer_6
  assign o[6] = e ? and_7_out : 1'bz;  // Controlled_Buffer controlled_buffer_7
  assign o[7] = e ? and_8_out : 1'bz;  // Controlled_Buffer controlled_buffer_8
endmodule

module cpu_reg_8 (
  input  [7:0] i,
  input  s,
  input  e,
  output [7:0] o,
  output [7:0] r
);

  cpu_mem_8 cpu_mem_8_1 (.i(i), .s(s), .out_3(r));
  cpu_eneb_8 cpu_eneb_8_1 (.i(r), .e(e), .o(o));

  // Notes on the sheet:
  //   s: initial=0x1
endmodule

module cpu_alu (
  input  [7:0] a,
  input  [7:0] b,
  input  carry_in,
  input  a1,
  input  b1,
  input  c1,
  output equal,
  output a_larger,
  output zero,
  output [7:0] o,
  output carry_out
);

  wire adder_1_cout, and_2_out, and_3_out, and_4_out, cpu_shl_1_shift_out, cpu_shr_1_shift_out,
       decoder_1_out0, decoder_1_out1, decoder_1_out2, decoder_1_out3, decoder_1_out4, decoder_1_out5,
       decoder_1_out6, or_2_out;
  wire [7:0] adder_1_out, and_1_out, cpu_shl_1_o, cpu_shr_1_o, cpu_xor_le_8_1_c, not_1_out, or_1_out;

  Adder adder_1 (.a(a), .b(b), .out(adder_1_out), .cin(carry_in), .cout(adder_1_cout));
  Decoder #(.select(3)) decoder_1 (
    .out0(decoder_1_out0), .out1(decoder_1_out1), .out2(decoder_1_out2), .out3(decoder_1_out3),
    .out4(decoder_1_out4), .out5(decoder_1_out5), .out6(decoder_1_out6), .sel({c1, b1, a1}));  // open: out7, en
  assign or_1_out = a | b;  // OR_Gate or_1, 8 bits wide
  assign and_1_out = a & b;  // AND_Gate and_1, 8 bits wide
  assign not_1_out = ~a;  // NOT_Gate not_1, 8 bits wide
  cpu_xor_le_8 cpu_xor_le_8_1 (.a(a), .b(b), .c(cpu_xor_le_8_1_c), .equal(equal), .larger(a_larger));
  cpu_shl cpu_shl_1 (.shift_in(carry_in), .i(a), .o(cpu_shl_1_o), .shift_out(cpu_shl_1_shift_out));
  cpu_shr cpu_shr_1 (.i(a), .shift_in(carry_in), .shift_out(cpu_shr_1_shift_out), .o(cpu_shr_1_o));
  cpu_eneb_8 cpu_eneb_8_1 (.i(cpu_xor_le_8_1_c), .e(decoder_1_out6), .o(o));
  cpu_eneb_8 cpu_eneb_8_2 (.i(or_1_out), .e(decoder_1_out5), .o(o));
  cpu_eneb_8 cpu_eneb_8_3 (.i(and_1_out), .e(decoder_1_out4), .o(o));
  cpu_eneb_8 cpu_eneb_8_4 (.i(not_1_out), .e(decoder_1_out3), .o(o));
  cpu_eneb_8 cpu_eneb_8_5 (.i(cpu_shl_1_o), .e(decoder_1_out2), .o(o));
  and and_2 (and_2_out, cpu_shr_1_shift_out, decoder_1_out1);
  and and_3 (and_3_out, cpu_shl_1_shift_out, decoder_1_out2);
  assign carry_out = decoder_1_out1 ? and_2_out : 1'bz;  // Controlled_Buffer controlled_buffer_1
  cpu_eneb_8 cpu_eneb_8_6 (.i(cpu_shr_1_o), .e(decoder_1_out1), .o(o));
  cpu_eneb_8 cpu_eneb_8_7 (.i(adder_1_out), .e(decoder_1_out0), .o(o));
  assign carry_out = decoder_1_out2 ? and_3_out : 1'bz;  // Controlled_Buffer controlled_buffer_2
  and and_4 (and_4_out, adder_1_cout, decoder_1_out0);
  assign carry_out = decoder_1_out0 ? and_4_out : 1'bz;  // Controlled_Buffer controlled_buffer_3
  or or_2 (or_2_out, o[0], o[1], o[2], o[3], o[4], o[5], o[6], o[7]);
  not not_2 (zero, or_2_out);
endmodule

module cpu_shr (
  input  [7:0] i,
  input  shift_in,
  output shift_out,
  output [7:0] o
);


  assign o = {shift_in, i[7:1]};
  assign shift_out = i[0];
endmodule

module cpu_shl (
  input  shift_in,
  input  [7:0] i,
  output [7:0] o,
  output shift_out
);


  assign o = {i[6:0], shift_in};
  assign shift_out = i[7];
endmodule

module cpu_xor_le_1 (
  input  a_larger,
  input  above_equal,
  input  a,
  input  b,
  output c,
  output equal,
  output a_large
);

  wire and_2_out, not_1_out;

  xor xor_1 (c, a, b);
  not not_1 (not_1_out, c);
  and and_1 (equal, not_1_out, above_equal);
  and and_2 (and_2_out, above_equal, a, c);
  or or_1 (a_large, and_2_out, a_larger);
endmodule

module cpu_xor_le_8 (
  input  [7:0] a,
  input  [7:0] b,
  output [7:0] c,
  output equal,
  output larger
);

  wire cpu_xor_le_1_1_a_large, cpu_xor_le_1_1_equal, cpu_xor_le_1_2_a_large, cpu_xor_le_1_2_equal,
       cpu_xor_le_1_3_a_large, cpu_xor_le_1_3_equal, cpu_xor_le_1_4_a_large, cpu_xor_le_1_4_equal,
       cpu_xor_le_1_5_a_large, cpu_xor_le_1_5_equal, cpu_xor_le_1_6_a_large, cpu_xor_le_1_6_equal,
       cpu_xor_le_1_7_a_large, cpu_xor_le_1_7_equal;

  cpu_xor_le_1 cpu_xor_le_1_1 (
    .a_larger(1'b0), .above_equal(1'b1), .a(a[0]), .b(b[0]), .c(c[0]), .equal(cpu_xor_le_1_1_equal),
    .a_large(cpu_xor_le_1_1_a_large));
  cpu_xor_le_1 cpu_xor_le_1_2 (
    .a_larger(cpu_xor_le_1_1_a_large), .above_equal(cpu_xor_le_1_1_equal), .a(a[1]), .b(b[1]), .c(c[1]),
    .equal(cpu_xor_le_1_2_equal), .a_large(cpu_xor_le_1_2_a_large));
  cpu_xor_le_1 cpu_xor_le_1_3 (
    .a_larger(cpu_xor_le_1_2_a_large), .above_equal(cpu_xor_le_1_2_equal), .a(a[2]), .b(b[2]), .c(c[2]),
    .equal(cpu_xor_le_1_3_equal), .a_large(cpu_xor_le_1_3_a_large));
  cpu_xor_le_1 cpu_xor_le_1_4 (
    .a_larger(cpu_xor_le_1_3_a_large), .above_equal(cpu_xor_le_1_3_equal), .a(a[3]), .b(b[3]), .c(c[3]),
    .equal(cpu_xor_le_1_4_equal), .a_large(cpu_xor_le_1_4_a_large));
  cpu_xor_le_1 cpu_xor_le_1_5 (
    .a_larger(cpu_xor_le_1_4_a_large), .above_equal(cpu_xor_le_1_4_equal), .a(a[4]), .b(b[4]), .c(c[4]),
    .equal(cpu_xor_le_1_5_equal), .a_large(cpu_xor_le_1_5_a_large));
  cpu_xor_le_1 cpu_xor_le_1_6 (
    .a_larger(cpu_xor_le_1_5_a_large), .above_equal(cpu_xor_le_1_5_equal), .a(a[5]), .b(b[5]), .c(c[5]),
    .equal(cpu_xor_le_1_6_equal), .a_large(cpu_xor_le_1_6_a_large));
  cpu_xor_le_1 cpu_xor_le_1_7 (
    .a_larger(cpu_xor_le_1_6_a_large), .above_equal(cpu_xor_le_1_6_equal), .a(a[6]), .b(b[6]), .c(c[6]),
    .equal(cpu_xor_le_1_7_equal), .a_large(cpu_xor_le_1_7_a_large));
  cpu_xor_le_1 cpu_xor_le_1_8 (
    .a_larger(cpu_xor_le_1_7_a_large), .above_equal(cpu_xor_le_1_7_equal), .a(a[7]), .b(b[7]), .c(c[7]),
    .equal(equal), .a_large(larger));
endmodule

module cpu (
  input  in_1,
  output [7:0] R0_RESULT,
  output [7:0] R1_RESULT,
  output [7:0] R2_RESULT,
  output [7:0] R3_RESULT,
  output [7:0] ACC_R,
  output [7:0] IAR_RESULT,
  output [7:0] out_8
);

  wire acc_e, acc_s, alu_1, alu_2, alu_3, bus_1, clock_1_out, cpu_alu_1_a_larger, cpu_alu_1_carry_out,
       cpu_alu_1_equal, cpu_alu_1_zero, cpu_clock_1_clk, cpu_clock_1_clk_e, cpu_clock_1_clk_s,
       cpu_control_section_2_1_r0_e, cpu_control_section_2_1_r0_s, cpu_control_section_2_1_r1_e,
       cpu_control_section_2_1_r1_s, cpu_control_section_2_1_r2_e, cpu_control_section_2_1_r2_s,
       cpu_control_section_2_1_r3_e, cpu_control_section_2_1_r3_s, cpu_flags_1_o_a, cpu_flags_1_o_c,
       cpu_flags_1_o_e, cpu_flags_1_o_z, flags_s, iar_e, iar_s, ir_s, mar_s, ram_e, ram_s, tmp_s;
  wire [7:0] cpu_alu_1_o, cpu_bus_1_1_o, cpu_ir_1_o, cpu_tmp_1_o;

  cpu_tmp cpu_tmp_1 (.i(out_8), .s(tmp_s), .o(cpu_tmp_1_o));
  cpu_bus_1 cpu_bus_1_1 (.i(cpu_tmp_1_o), .bus_1(bus_1), .o(cpu_bus_1_1_o));
  cpu_alu cpu_alu_1 (
    .a(out_8), .b(cpu_bus_1_1_o), .carry_in(in_1), .a1(alu_1), .b1(alu_2), .c1(alu_3),
    .equal(cpu_alu_1_equal), .a_larger(cpu_alu_1_a_larger), .zero(cpu_alu_1_zero), .o(cpu_alu_1_o),
    .carry_out(cpu_alu_1_carry_out));
  cpu_acc cpu_acc_1 (.i(cpu_alu_1_o), .s(acc_s), .e(acc_e), .o(out_8), .r(ACC_R));
  Clock clock_1 (.out(clock_1_out));
  // Probe on out_8
  cpu_clock cpu_clock_1 (
    .in_1(clock_1_out), .clk(cpu_clock_1_clk), .clk_s(cpu_clock_1_clk_s), .clk_e(cpu_clock_1_clk_e));
  cpu_flags cpu_flags_1 (
    .c(cpu_alu_1_carry_out), .a(cpu_alu_1_a_larger), .e(cpu_alu_1_equal), .z(cpu_alu_1_zero), .s(flags_s),
    .o_c(cpu_flags_1_o_c), .o_a(cpu_flags_1_o_a), .o_e(cpu_flags_1_o_e), .o_z(cpu_flags_1_o_z));
  cpu_ir cpu_ir_1 (.i(out_8), .s(ir_s), .o(cpu_ir_1_o));
  cpu_control_section_2 cpu_control_section_2_1 (
    .clk(cpu_clock_1_clk), .clk_s(cpu_clock_1_clk_s), .clk_e(cpu_clock_1_clk_e), .carry_out(cpu_flags_1_o_c),
    .a_larger(cpu_flags_1_o_a), .equal(cpu_flags_1_o_e), .zero(cpu_flags_1_o_z), .IR_IN(cpu_ir_1_o),
    .bus_1(bus_1), .IR_S(ir_s), .IAR_E(iar_e), .MAR_S(mar_s), .RAM_E(ram_e), .IAR_S(iar_s), .ACC_E(acc_e),
    .ACC_S(acc_s), .RAM_S(ram_s), .TMP_S(tmp_s), .FLAGS_S(flags_s), .R0_E(cpu_control_section_2_1_r0_e),
    .R0_S(cpu_control_section_2_1_r0_s), .R1_E(cpu_control_section_2_1_r1_e),
    .R1_S(cpu_control_section_2_1_r1_s), .R2_E(cpu_control_section_2_1_r2_e),
    .R2_S(cpu_control_section_2_1_r2_s), .R3_E(cpu_control_section_2_1_r3_e),
    .R3_S(cpu_control_section_2_1_r3_s), .ALU_1(alu_1), .ALU_2(alu_2), .ALU_3(alu_3));
  cpu_iar cpu_iar_1 (.i(out_8), .s(iar_s), .e(iar_e), .o(out_8), .r(IAR_RESULT));
  cpu_reg_8 cpu_reg_8_1 (
    .i(out_8), .s(cpu_control_section_2_1_r0_s), .e(cpu_control_section_2_1_r0_e), .o(out_8), .r(R0_RESULT));
  cpu_reg_8 cpu_reg_8_2 (
    .i(out_8), .s(cpu_control_section_2_1_r1_s), .e(cpu_control_section_2_1_r1_e), .o(out_8), .r(R1_RESULT));
  cpu_reg_8 cpu_reg_8_3 (
    .i(out_8), .s(cpu_control_section_2_1_r2_s), .e(cpu_control_section_2_1_r2_e), .o(out_8), .r(R2_RESULT));
  cpu_reg_8 cpu_reg_8_4 (
    .i(out_8), .s(cpu_control_section_2_1_r3_s), .e(cpu_control_section_2_1_r3_e), .o(out_8), .r(R3_RESULT));
  cpu_ram cpu_ram_1 (.address(out_8), .sa(mar_s), .s(ram_s), .e(ram_e), .data(out_8), .o(out_8));
endmodule

module cpu_tmp (
  input  [7:0] i,
  input  s,
  output [7:0] o
);

  cpu_mem_8 cpu_mem_8_1 (.i(i), .s(s), .out_3(o));
endmodule

module cpu_bus_1 (
  input  [7:0] i,
  input  bus_1,
  output [7:0] o
);

  wire not_1_out;

  not not_1 (not_1_out, bus_1);
  or or_1 (o[0], i[0], bus_1);
  and and_1 (o[1], i[1], not_1_out);
  and and_2 (o[2], i[2], not_1_out);
  and and_3 (o[3], i[3], not_1_out);
  and and_4 (o[4], i[4], not_1_out);
  and and_5 (o[5], i[5], not_1_out);
  and and_6 (o[6], i[6], not_1_out);
  and and_7 (o[7], i[7], not_1_out);
endmodule

module cpu_ram (
  input  [7:0] address,
  input  sa,
  input  s,
  input  e,
  input  [7:0] data,
  output [7:0] o
);

  wire [7:0] cpu_eneb_8_1_o, cpu_mem_8_1_out_3, ram_1_dout;

  cpu_mem_8 cpu_mem_8_1 (.i(address), .s(sa), .out_3(cpu_mem_8_1_out_3));
  RAM #(.enables("line")) ram_1 (.addr(cpu_mem_8_1_out_3), .we(1'b1), .clk(s), .din(data), .dout(ram_1_dout));
  cpu_eneb_8 cpu_eneb_8_1 (.i(ram_1_dout), .e(e), .o(cpu_eneb_8_1_o));
  assign o = e ? cpu_eneb_8_1_o : 8'bz;  // Controlled_Buffer controlled_buffer_1
endmodule

module cpu_control_section (
  input  clk,
  input  clk_s,
  input  clk_e,
  input  carry_out,
  input  a_larger,
  input  equal,
  input  zero,
  input  [7:0] ir_in,
  output ir_s,
  output tmp_s,
  output bus_1,
  output mar_s,
  output acc_e,
  output acc_s,
  output iar_s,
  output iar_e,
  output ram_s,
  output ram_e,
  output R0_e,
  output R0_s,
  output R1_e,
  output R1_s,
  output R2_e,
  output R2_s,
  output R3_e,
  output R3_s,
  output flags_s,
  output ALU_1,
  output ALU_2,
  output ALU_3
);

  wire acc_e_1, acc_e_3, acc_e_6, acc_s_1, acc_s_3, acc_s_6, and_4_out, and_5_out, and_6_out, and_7_out,
       and_8_out, and_9_out, and_10_out, and_11_out, and_16_out, and_17_out, and_18_out, and_19_out,
       and_20_out, and_34_out, and_35_out, and_36_out, and_37_out, and_38_out, and_39_out, and_40_out,
       bus_1_7, decoder_1_out0, decoder_1_out1, decoder_1_out2, decoder_1_out3, decoder_2_out0,
       decoder_2_out1, decoder_2_out2, decoder_2_out3, decoder_3_out0, decoder_3_out1, decoder_3_out2,
       decoder_3_out6, decoder_4_out0, decoder_4_out1, decoder_4_out2, decoder_4_out3, decoder_5_out0,
       decoder_5_out1, decoder_5_out2, decoder_5_out3, decoder_5_out4, decoder_5_out5, decoder_5_out6,
       decoder_5_out7, iar_e_5, iar_s_4, iar_s_5, iar_s_6_2, mar_s_2, mar_s_2_2, not_1_out, not_2_out,
       or_6_out, or_7_out, or_8_out, or_9_out, or_10_out, or_11_out, or_12_out, or_13_out, or_14_out,
       or_15_out, ram_e_2, ram_e_3, ram_s_2, reg_B_e_1, step_4, step_5, step_6;
  wire [2:0] counter_1_q;

  or or_1 (R0_e, and_4_out, and_8_out);
  or or_2 (R1_e, and_5_out, and_9_out);
  or or_3 (R2_e, and_6_out, and_10_out);
  or or_4 (R3_e, and_7_out, and_11_out);
  or or_5 (bus_1, decoder_3_out0, acc_s_3, acc_s_6, bus_1_7);
  and and_1 (acc_e, clk_e, or_6_out);
  and and_2 (iar_e, clk_e, or_7_out);
  and and_3 (ram_e, clk_e, or_8_out);
  and and_4 (and_4_out, clk_e, or_9_out, decoder_1_out0);
  and and_5 (and_5_out, clk_e, or_9_out, decoder_1_out1);
  and and_6 (and_6_out, clk_e, or_9_out, decoder_1_out2);
  and and_7 (and_7_out, clk_e, or_9_out, decoder_1_out3);
  and and_8 (and_8_out, clk_e, or_10_out, decoder_2_out0);
  and and_9 (and_9_out, clk_e, or_10_out, decoder_2_out1);
  and and_10 (and_10_out, clk_e, or_10_out, decoder_2_out2);
  and and_11 (and_11_out, clk_e, or_10_out, decoder_2_out3);
  or or_6 (or_6_out, decoder_3_out2, acc_e_1, acc_e_3, acc_e_6);
  or or_7 (or_7_out, decoder_3_out0, acc_s_3, iar_e_5, acc_s_6);
  or or_8 (or_8_out, decoder_3_out1, ram_e_2, iar_s_6_2, ram_e_3, iar_s_5);
  or or_9 (or_9_out, reg_B_e_1, ram_s_2, iar_s_4);
  or or_10 (or_10_out, acc_s_1, mar_s_2, mar_s_2_2);
  Decoder #(.select(2)) decoder_1 (
    .out0(decoder_1_out0), .out1(decoder_1_out1), .out2(decoder_1_out2), .out3(decoder_1_out3),
    .sel(ir_in[1:0]));  // open: en
  Decoder #(.select(2)) decoder_2 (
    .out0(decoder_2_out0), .out1(decoder_2_out1), .out2(decoder_2_out2), .out3(decoder_2_out3),
    .sel(ir_in[3:2]));  // open: en
  and and_12 (ALU_1, step_5, ir_in[7], ir_in[4]);
  and and_13 (ALU_2, step_5, ir_in[7], ir_in[5]);
  and and_14 (ALU_3, step_5, ir_in[7], ir_in[6]);
  Counter #(.max('h7), .trigger("falling"), .width(3)) counter_1 (
    .Q(counter_1_q), .clk(clk), .clr(decoder_3_out6));  // open: load, D, count, carry, up
  Decoder #(.select(3)) decoder_3 (
    .out0(decoder_3_out0), .out1(decoder_3_out1), .out2(decoder_3_out2), .out3(step_4), .out4(step_5),
    .out5(step_6), .out6(decoder_3_out6), .sel(counter_1_q));  // open: out7, en
  and and_15 (reg_B_e_1, step_4, ir_in[7]);
  and and_16 (and_16_out, carry_out, ir_in[3]);
  and and_17 (and_17_out, a_larger, ir_in[2]);
  and and_18 (and_18_out, equal, ir_in[1]);
  and and_19 (and_19_out, zero, ir_in[0]);
  or or_11 (or_11_out, and_16_out, and_17_out, and_18_out, and_19_out);
  and and_20 (and_20_out, ir_in[4], ir_in[5], ir_in[6]);
  and and_21 (acc_s_1, step_5, ir_in[7]);
  not not_1 (not_1_out, and_20_out);
  and and_22 (acc_e_1, step_6, ir_in[7], not_1_out);
  Decoder #(.select(2)) decoder_4 (
    .out0(decoder_4_out0), .out1(decoder_4_out1), .out2(decoder_4_out2), .out3(decoder_4_out3),
    .sel(ir_in[1:0]));  // open: en
  or or_12 (or_12_out, acc_e_1, ram_e_2, ram_e_3);
  or or_13 (or_13_out, iar_e_5, decoder_3_out0, mar_s_2, mar_s_2_2, acc_s_3, acc_s_6);
  or or_14 (or_14_out, decoder_3_out0, acc_s_1, acc_s_3, acc_s_6);
  or or_15 (or_15_out, acc_e_6, decoder_3_out2, acc_e_3, iar_s_4, iar_s_5, iar_s_6_2);
  not not_2 (not_2_out, ir_in[7]);
  and and_23 (ir_s, clk_s, decoder_3_out1);
  and and_24 (tmp_s, clk_s, reg_B_e_1);
  and and_25 (mar_s, clk_s, or_13_out);
  and and_26 (acc_s, clk_s, or_14_out);
  and and_27 (iar_s, clk_s, or_15_out);
  and and_28 (ram_s, clk_s, ram_s_2);
  and and_29 (R0_s, clk_s, or_12_out, decoder_4_out0);
  and and_30 (R1_s, clk_s, or_12_out, decoder_4_out1);
  and and_31 (R2_s, clk_s, or_12_out, decoder_4_out2);
  and and_32 (R3_s, clk_s, or_12_out, decoder_4_out3);
  and and_33 (flags_s, bus_1_7, clk_s);
  Decoder #(.select(3)) decoder_5 (
    .out0(decoder_5_out0), .out1(decoder_5_out1), .out2(decoder_5_out2), .out3(decoder_5_out3),
    .out4(decoder_5_out4), .out5(decoder_5_out5), .out6(decoder_5_out6), .out7(decoder_5_out7),
    .sel(ir_in[6:4]));  // open: en
  and and_34 (and_34_out, decoder_5_out0, not_2_out);
  and and_35 (and_35_out, decoder_5_out1, not_2_out);
  and and_36 (and_36_out, decoder_5_out2, not_2_out);
  and and_37 (and_37_out, decoder_5_out3, not_2_out);
  and and_38 (and_38_out, decoder_5_out4, not_2_out);
  and and_39 (and_39_out, decoder_5_out5, not_2_out);
  and and_40 (and_40_out, decoder_5_out6, not_2_out);
  // AND_Gate and_41 has open pins: in0=decoder_5_out7, in1=not_2_out, out=open
  and and_42 (mar_s_2, step_4, and_34_out);
  and and_43 (mar_s_2_2, step_4, and_35_out);
  and and_44 (ram_e_2, step_5, and_34_out);
  and and_45 (ram_s_2, step_5, and_35_out);
  and and_46 (acc_s_3, step_4, and_36_out);
  and and_47 (ram_e_3, step_5, and_36_out);
  and and_48 (acc_e_3, step_6, and_36_out);
  and and_49 (iar_s_4, step_4, and_37_out);
  and and_50 (iar_e_5, step_4, and_38_out);
  and and_51 (iar_s_5, step_5, and_38_out);
  and and_52 (acc_s_6, step_4, and_39_out);
  and and_53 (acc_e_6, step_5, and_39_out);
  and and_54 (iar_s_6_2, step_6, and_39_out, or_11_out);
  and and_55 (bus_1_7, step_4, and_40_out);

  // Other names for the same wires on the sheet: flags_s_7 = bus_1_7; iar_s_3 = acc_e_3; iar_s_6 = acc_e_6;
  //   bus_1_3 = acc_s_3; iar_e_3 = acc_s_3; mar_s_3 = acc_s_3; mar_s_5 = iar_e_5; bus_1_6 = acc_s_6;
  //   iar_e_6 = acc_s_6; mar_s_6 = acc_s_6; ram_e_5 = iar_s_5; ram_e_6 = iar_s_6_2; reg_A_e_1 = acc_s_1;
  //   reg_A_e_2 = mar_s_2; reg_A_e_2_2 = mar_s_2_2; reg_B_e_2 = ram_s_2; reg_B_e_4 = iar_s_4; reg_B_s_1 = acc_e_1;
  //   reg_B_s_2 = ram_e_2; reg_B_s_3 = ram_e_3; tmp_s_1 = reg_B_e_1

  // Notes on the sheet:
  //   Первые три шага
  //   и увеличивем счетчик на один
  //   это мы вытаскиваем инструкцию
  //   Steps
  //   1
  //   1
  //   2
  //   3
  //   4
  //   4
  //   5
  //   5
  //   6
  //   6
  //   2
  //   Загружаем данные из памяти в регистр по указаному в регистре А адресу
  //   Загружаем данные из регистра в память по указанному в регистре А адресу
  //   3
  //   Загрузка данных из соседнего байта
  //   4
  //   5
  //   6
  //   7
endmodule

module cpu_stepper (
  input  reset,
  input  clk,
  output s1,
  output s2,
  output s3,
  output s4,
  output s5,
  output s6,
  output s7
);

  wire cpu_mem_1_1_o, cpu_mem_1_2_o, cpu_mem_1_3_o, cpu_mem_1_4_o, cpu_mem_1_5_o, cpu_mem_1_6_o,
       cpu_mem_1_7_o, cpu_mem_1_9_o, cpu_mem_1_10_o, cpu_mem_1_11_o, cpu_mem_1_12_o, not_1_out, not_2_out,
       not_3_out, not_4_out, not_5_out, not_6_out, not_7_out, not_8_out, or_1_out, or_2_out;

  not not_1 (not_1_out, clk);
  or or_1 (or_1_out, reset, clk);
  or or_2 (or_2_out, reset, not_1_out);
  not not_2 (not_2_out, reset);
  or or_3 (s1, reset, not_3_out);
  not not_3 (not_3_out, cpu_mem_1_3_o);
  cpu_mem_1 cpu_mem_1_1 (.i(not_2_out), .s(or_1_out), .o(cpu_mem_1_1_o));
  cpu_mem_1 cpu_mem_1_2 (.i(cpu_mem_1_12_o), .s(or_1_out), .o(cpu_mem_1_2_o));
  and and_1 (s2, cpu_mem_1_3_o, not_4_out);
  not not_4 (not_4_out, cpu_mem_1_7_o);
  and and_2 (s3, cpu_mem_1_7_o, not_5_out);
  not not_5 (not_5_out, cpu_mem_1_10_o);
  cpu_mem_1 cpu_mem_1_3 (.i(cpu_mem_1_1_o), .s(or_2_out), .o(cpu_mem_1_3_o));
  cpu_mem_1 cpu_mem_1_4 (.i(cpu_mem_1_2_o), .s(or_2_out), .o(cpu_mem_1_4_o));
  and and_3 (s4, cpu_mem_1_10_o, not_6_out);
  not not_6 (not_6_out, cpu_mem_1_12_o);
  and and_4 (s5, cpu_mem_1_12_o, not_7_out);
  cpu_mem_1 cpu_mem_1_5 (.i(cpu_mem_1_3_o), .s(or_1_out), .o(cpu_mem_1_5_o));
  cpu_mem_1 cpu_mem_1_6 (.i(cpu_mem_1_4_o), .s(or_1_out), .o(cpu_mem_1_6_o));
  not not_7 (not_7_out, cpu_mem_1_4_o);
  and and_5 (s6, cpu_mem_1_4_o, not_8_out);
  not not_8 (not_8_out, s7);
  cpu_mem_1 cpu_mem_1_7 (.i(cpu_mem_1_5_o), .s(or_2_out), .o(cpu_mem_1_7_o));
  cpu_mem_1 cpu_mem_1_8 (.i(cpu_mem_1_6_o), .s(or_2_out), .o(s7));
  cpu_mem_1 cpu_mem_1_9 (.i(cpu_mem_1_7_o), .s(or_1_out), .o(cpu_mem_1_9_o));
  cpu_mem_1 cpu_mem_1_10 (.i(cpu_mem_1_9_o), .s(or_2_out), .o(cpu_mem_1_10_o));
  cpu_mem_1 cpu_mem_1_11 (.i(cpu_mem_1_10_o), .s(or_1_out), .o(cpu_mem_1_11_o));
  cpu_mem_1 cpu_mem_1_12 (.i(cpu_mem_1_11_o), .s(or_2_out), .o(cpu_mem_1_12_o));
endmodule

module cpu_clock (
  input  in_1,
  output clk,
  output clk_s,
  output clk_e
);

  wire j_k_ff_1_qn, nand_1_out;

  J_K_Flip_Flop j_k_ff_1 (.J(1'b1), .K(1'b1), .clk(in_1), .Q(clk), .Qn(j_k_ff_1_qn));  // open: preset, reset
  nand nand_1 (nand_1_out, in_1, clk);
  nand nand_2 (clk_e, j_k_ff_1_qn, in_1);
  not not_1 (clk_s, nand_1_out);
endmodule

module cpu_acc (
  input  [7:0] i,
  input  s,
  input  e,
  output [7:0] o,
  output [7:0] r
);

  cpu_reg_8 cpu_reg_8_1 (.i(i), .s(s), .e(e), .o(o), .r(r));
endmodule

module cpu_ir (
  input  [7:0] i,
  input  s,
  output [7:0] o
);

  cpu_mem_8 cpu_mem_8_1 (.i(i), .s(s), .out_3(o));
endmodule

// adress of instr
module cpu_iar (
  input  [7:0] i,
  input  s,
  input  e,
  output [7:0] o,
  output [7:0] r
);

  cpu_reg_8 cpu_reg_8_1 (.i(i), .s(s), .e(e), .o(o), .r(r));

  // Notes on the sheet:
  //   s: initial=0x1
endmodule

module cpu_flags (
  input  c,
  input  a,
  input  e,
  input  z,
  input  s,
  output o_c,
  output o_a,
  output o_e,
  output o_z
);

  cpu_mem_1 cpu_mem_1_1 (.i(c), .s(s), .o(o_c));
  cpu_mem_1 cpu_mem_1_2 (.i(a), .s(s), .o(o_a));
  cpu_mem_1 cpu_mem_1_3 (.i(e), .s(s), .o(o_e));
  cpu_mem_1 cpu_mem_1_4 (.i(z), .s(s), .o(o_z));
endmodule

module cpu_control_section_2 (
  input  clk,
  input  clk_s,
  input  clk_e,
  input  carry_out,
  input  a_larger,
  input  equal,
  input  zero,
  input  [7:0] IR_IN,
  output bus_1,
  output IR_S,
  output IAR_E,
  output MAR_S,
  output RAM_E,
  output IAR_S,
  output ACC_E,
  output ACC_S,
  output RAM_S,
  output TMP_S,
  output FLAGS_S,
  output R0_E,
  output R0_S,
  output R1_E,
  output R1_S,
  output R2_E,
  output R2_S,
  output R3_E,
  output R3_S,
  output ALU_1,
  output ALU_2,
  output ALU_3
);

  wire and_1_out, and_2_out, and_3_out, and_4_out, and_5_out, and_6_out, and_7_out, and_8_out, and_12_out,
       and_13_out, and_14_out, and_15_out, and_16_out, and_17_out, and_18_out, and_20_out, and_21_out,
       and_22_out, and_23_out, and_24_out, and_25_out, and_26_out, and_27_out, and_28_out, and_29_out,
       and_30_out, and_31_out, and_32_out, and_33_out, and_34_out, and_35_out, and_36_out, and_37_out,
       and_38_out, and_39_out, and_40_out, and_41_out, decoder_1_out0, decoder_1_out1, decoder_1_out2,
       decoder_1_out3, decoder_2_out0, decoder_2_out1, decoder_2_out2, decoder_2_out3, decoder_3_out0,
       decoder_3_out1, decoder_3_out2, decoder_3_out3, decoder_3_out4, decoder_3_out5, decoder_3_out6,
       decoder_3_out7, decoder_4_out0, decoder_4_out1, decoder_4_out2, decoder_4_out3, decoder_4_out5,
       decoder_4_out6, decoder_5_out0, decoder_5_out1, decoder_5_out2, decoder_5_out3, not_1_out, not_2_out,
       or_9_out, or_10_out, or_11_out, or_12_out, or_13_out, REG_A_E_out, REG_B_E_out, REG_B_S_out, step_5;
  wire [2:0] counter_1_q;

  or or_1 (R0_E, and_1_out, and_5_out);
  or or_2 (R1_E, and_2_out, and_6_out);
  or or_3 (R2_E, and_3_out, and_7_out);
  or or_4 (R3_E, and_4_out, and_8_out);
  and and_1 (and_1_out, clk_e, decoder_1_out0, REG_B_E_out);
  and and_2 (and_2_out, clk_e, decoder_1_out1, REG_B_E_out);
  and and_3 (and_3_out, clk_e, decoder_1_out2, REG_B_E_out);
  and and_4 (and_4_out, clk_e, decoder_1_out3, REG_B_E_out);
  and and_5 (and_5_out, clk_e, decoder_2_out0, REG_A_E_out);
  and and_6 (and_6_out, clk_e, decoder_2_out1, REG_A_E_out);
  and and_7 (and_7_out, clk_e, decoder_2_out2, REG_A_E_out);
  and and_8 (and_8_out, clk_e, decoder_2_out3, REG_A_E_out);
  or REG_B_E (REG_B_E_out, and_24_out, and_35_out, and_28_out, 1'b0);
  or REG_A_E (REG_A_E_out, and_33_out, and_26_out, and_25_out);
  and and_9 (ALU_1, step_5, IR_IN[4], IR_IN[7]);
  and and_10 (ALU_2, step_5, IR_IN[5], IR_IN[7]);
  and and_11 (ALU_3, step_5, IR_IN[6], IR_IN[7]);
  or or_5 (bus_1, decoder_4_out0, and_27_out, and_30_out, and_31_out);
  or or_6 (IAR_E, decoder_4_out0, and_29_out, and_27_out, and_30_out);
  or or_7 (RAM_E, decoder_4_out1, and_36_out, and_41_out, and_37_out, and_34_out);
  or or_8 (ACC_E, decoder_4_out2, and_40_out, and_38_out, and_39_out);
  Decoder #(.select(2)) decoder_1 (
    .out0(decoder_1_out0), .out1(decoder_1_out1), .out2(decoder_1_out2), .out3(decoder_1_out3),
    .sel(IR_IN[1:0]));  // open: en
  Decoder #(.select(2)) decoder_2 (
    .out0(decoder_2_out0), .out1(decoder_2_out1), .out2(decoder_2_out2), .out3(decoder_2_out3),
    .sel(IR_IN[3:2]));  // open: en
  Decoder #(.select(3)) decoder_3 (
    .out0(decoder_3_out0), .out1(decoder_3_out1), .out2(decoder_3_out2), .out3(decoder_3_out3),
    .out4(decoder_3_out4), .out5(decoder_3_out5), .out6(decoder_3_out6), .out7(decoder_3_out7),
    .sel(IR_IN[6:4]));  // open: en
  not not_1 (not_1_out, IR_IN[7]);
  and and_12 (and_12_out, decoder_3_out0, not_1_out);
  and and_13 (and_13_out, decoder_3_out1, not_1_out);
  and and_14 (and_14_out, decoder_3_out2, not_1_out);
  and and_15 (and_15_out, decoder_3_out3, not_1_out);
  and and_16 (and_16_out, decoder_3_out4, not_1_out);
  and and_17 (and_17_out, decoder_3_out5, not_1_out);
  and and_18 (and_18_out, decoder_3_out6, not_1_out);
  // AND_Gate and_19 has open pins: in0=decoder_3_out7, in1=not_1_out, out=open
  and and_20 (and_20_out, carry_out, IR_IN[3]);
  and and_21 (and_21_out, a_larger, IR_IN[2]);
  and and_22 (and_22_out, equal, IR_IN[1]);
  and and_23 (and_23_out, zero, IR_IN[0]);
  Counter #(.max('h7), .trigger("falling"), .width(3)) counter_1 (
    .Q(counter_1_q), .clk(clk), .clr(decoder_4_out6));  // open: load, D, count, carry, up
  Decoder #(.select(3)) decoder_4 (
    .out0(decoder_4_out0), .out1(decoder_4_out1), .out2(decoder_4_out2), .out3(decoder_4_out3),
    .out4(step_5), .out5(decoder_4_out5), .out6(decoder_4_out6), .sel(counter_1_q));  // open: out7, en
  and and_24 (and_24_out, decoder_4_out3, IR_IN[7]);
  and and_25 (and_25_out, decoder_4_out3, and_12_out);
  and and_26 (and_26_out, decoder_4_out3, and_13_out);
  and and_27 (and_27_out, decoder_4_out3, and_14_out);
  and and_28 (and_28_out, decoder_4_out3, and_15_out);
  and and_29 (and_29_out, decoder_4_out3, and_16_out);
  and and_30 (and_30_out, decoder_4_out3, and_17_out);
  and and_31 (and_31_out, decoder_4_out3, and_18_out);
  or or_9 (or_9_out, and_20_out, and_21_out, and_22_out, and_23_out);
  and and_32 (and_32_out, IR_IN[4], IR_IN[5], IR_IN[6]);
  not not_2 (not_2_out, and_32_out);
  and and_33 (and_33_out, step_5, IR_IN[7]);
  and and_34 (and_34_out, step_5, and_12_out);
  and and_35 (and_35_out, step_5, and_13_out);
  and and_36 (and_36_out, step_5, and_14_out);
  and and_37 (and_37_out, step_5, and_16_out);
  and and_38 (and_38_out, step_5, and_17_out);
  and and_39 (and_39_out, decoder_4_out5, not_2_out, IR_IN[7]);
  and and_40 (and_40_out, decoder_4_out5, and_14_out);
  and and_41 (and_41_out, decoder_4_out5, or_9_out, and_17_out);
  Decoder #(.select(2)) decoder_5 (
    .out0(decoder_5_out0), .out1(decoder_5_out1), .out2(decoder_5_out2), .out3(decoder_5_out3),
    .sel(IR_IN[1:0]));  // open: en
  or or_10 (or_10_out, and_29_out, decoder_4_out0, and_26_out, and_27_out, and_25_out, and_30_out);
  or or_11 (or_11_out, and_41_out, and_40_out, and_28_out, and_37_out, decoder_4_out2, and_38_out);
  or or_12 (or_12_out, decoder_4_out0, and_27_out, and_30_out, and_33_out);
  or or_13 (or_13_out, and_31_out, and_33_out);
  or REG_B_S (REG_B_S_out, and_39_out, and_36_out, and_34_out);
  and and_42 (IR_S, clk_s, decoder_4_out1);
  and and_43 (MAR_S, clk_s, or_10_out);
  and and_44 (IAR_S, clk_s, or_11_out);
  and and_45 (ACC_S, clk_s, or_12_out);
  and and_46 (RAM_S, clk_s, and_35_out);
  and and_47 (TMP_S, clk_s, and_24_out);
  and and_48 (FLAGS_S, clk_s, or_13_out);
  and and_49 (R0_S, decoder_5_out0, REG_B_S_out, clk_s);
  and and_50 (R1_S, decoder_5_out1, REG_B_S_out, clk_s);
  and and_51 (R2_S, decoder_5_out2, REG_B_S_out, clk_s);
  and and_52 (R3_S, decoder_5_out3, REG_B_S_out, clk_s);

  // Notes on the sheet:
  //   REG_B
  //   REG_A
  //   Enable
  //   SET
endmodule
